// Logisim project Classical_CPU_final.circ as structural Verilog: 29 circuits, main circuit main
module main (
  input  in8,
  input  in7,
  input  in6,
  input  in5,
  input  in4,
  input  in3,
  input  in2,
  input  in1,
  input  clk,
  input  readwrite,
  input  addr1,
  input  addr2,
  input  addr3,
  input  addr4,
  output out8,
  output out7,
  output out6,
  output out5,
  output out4,
  output out3,
  output out2,
  output out1
);

  wire a0000_outeight, a0000_outfive, a0000_outfour, a0000_outone, a0000_outseven, a0000_outsix,
       a0000_outthree, a0000_outtwo, a0001_outeight, a0001_outfive, a0001_outfour, a0001_outone,
       a0001_outseven, a0001_outsix, a0001_outthree, a0001_outtwo, a0010_outeight, a0010_outfive,
       a0010_outfour, a0010_outone, a0010_outseven, a0010_outsix, a0010_outthree, a0010_outtwo, and_1_out,
       and_2_out, and_3_out, and_4_out, and_5_out, and_6_out, and_7_out, and_8_out, and_9_out, and_10_out,
       and_11_out, and_12_out, and_13_out, and_14_out, and_15_out, and_16_out, and_17_out, and_18_out,
       and_19_out, and_20_out, and_21_out, and_22_out, and_23_out, and_24_out, and_25_out, and_26_out,
       and_27_out, and_28_out, and_29_out, and_30_out, and_31_out, and_32_out, and_33_out, and_34_out,
       and_35_out, and_36_out, and_37_out, and_38_out, and_39_out, and_40_out, eight_out, eleven_out,
       fifteen_out, five_out, four_out, fourteen_out, nine_out, not_1_out, not_2_out, not_3_out, not_4_out,
       not_5_out, not_6_out, not_7_out, not_8_out, not_9_out, not_10_out, not_11_out, not_12_out, not_13_out,
       not_14_out, not_15_out, not_16_out, not_17_out, not_18_out, not_19_out, not_20_out, not_21_out,
       not_22_out, not_23_out, not_24_out, not_25_out, not_26_out, not_27_out, not_28_out, not_29_out,
       not_30_out, not_31_out, not_32_out, not_33_out, not_34_out, not_35_out, not_36_out, not_37_out,
       not_38_out, not_39_out, not_40_out, not_41_out, not_42_out, not_43_out, not_44_out, not_45_out,
       not_46_out, not_47_out, not_48_out, not_49_out, not_50_out, not_51_out, not_52_out, not_53_out,
       not_54_out, not_55_out, not_56_out, not_57_out, one_byte_1_outeight, one_byte_1_outfive,
       one_byte_1_outfour, one_byte_1_outone, one_byte_1_outseven, one_byte_1_outsix, one_byte_1_outthree,
       one_byte_1_outtwo, one_byte_2_outeight, one_byte_2_outfive, one_byte_2_outfour, one_byte_2_outone,
       one_byte_2_outseven, one_byte_2_outsix, one_byte_2_outthree, one_byte_2_outtwo, one_byte_3_outeight,
       one_byte_3_outfive, one_byte_3_outfour, one_byte_3_outone, one_byte_3_outseven, one_byte_3_outsix,
       one_byte_3_outthree, one_byte_3_outtwo, one_byte_4_outeight, one_byte_4_outfive, one_byte_4_outfour,
       one_byte_4_outone, one_byte_4_outseven, one_byte_4_outsix, one_byte_4_outthree, one_byte_4_outtwo,
       one_byte_5_outeight, one_byte_5_outfive, one_byte_5_outfour, one_byte_5_outseven, one_byte_5_outsix,
       one_byte_5_outthree, one_byte_5_outtwo, one_byte_6_outeight, one_byte_6_outfive, one_byte_6_outfour,
       one_byte_6_outone, one_byte_6_outseven, one_byte_6_outsix, one_byte_6_outthree, one_byte_6_outtwo,
       one_byte_7_outeight, one_byte_7_outfive, one_byte_7_outfour, one_byte_7_outone, one_byte_7_outseven,
       one_byte_7_outthree, one_byte_7_outtwo, one_byte_8_outeight, one_byte_8_outfive, one_byte_8_outfour,
       one_byte_8_outone, one_byte_8_outseven, one_byte_8_outsix, one_byte_8_outthree, one_byte_8_outtwo,
       one_byte_9_outeight, one_byte_9_outfive, one_byte_9_outfour, one_byte_9_outone, one_byte_9_outseven,
       one_byte_9_outsix, one_byte_9_outthree, one_byte_9_outtwo, one_byte_10_outeight, one_byte_10_outfive,
       one_byte_10_outfour, one_byte_10_outone, one_byte_10_outseven, one_byte_10_outsix,
       one_byte_10_outthree, one_byte_10_outtwo, one_byte_11_outeight, one_byte_11_outfive,
       one_byte_11_outfour, one_byte_11_outone, one_byte_11_outseven, one_byte_11_outsix,
       one_byte_11_outthree, one_byte_11_outtwo, one_out, or_1_out, or_2_out, or_3_out, or_4_out, or_5_out,
       or_6_out, or_7_out, or_8_out, ppppp_outeight, ppppp_outfive, ppppp_outfour, ppppp_outone,
       ppppp_outseven, ppppp_outsix, ppppp_outthree, ppppp_outtwo, s_r_ff_1_q, s_r_ff_2_q, s_r_ff_3_q,
       s_r_ff_4_q, s_r_ff_5_q, s_r_ff_6_q, s_r_ff_7_q, s_r_ff_8_q, s_r_ff_9_q, s_r_ff_10_q, s_r_ff_11_q,
       s_r_ff_12_q, s_r_ff_13_q, s_r_ff_14_q, s_r_ff_15_q, s_r_ff_16_q, seven_out, six_out, sixteen_out,
       ten_out, thirdteen_out, three_out, twelve_out, two_out, undriven, undriven_2, undriven_3, undriven_4;

  not not_1 (not_1_out, addr1);
  and one (one_out, addr3, addr1, addr4, addr2);
  not not_2 (not_2_out, addr1);
  not not_3 (not_3_out, addr4);
  not not_4 (not_4_out, addr1);
  not not_5 (not_5_out, addr3);
  not not_6 (not_6_out, addr1);
  not not_7 (not_7_out, addr2);
  not not_8 (not_8_out, addr3);
  not not_9 (not_9_out, addr4);
  not not_10 (not_10_out, addr1);
  not not_11 (not_11_out, addr2);
  not not_12 (not_12_out, addr3);
  not not_13 (not_13_out, addr1);
  not not_14 (not_14_out, addr2);
  not not_15 (not_15_out, addr4);
  not not_16 (not_16_out, addr1);
  not not_17 (not_17_out, addr2);
  not not_18 (not_18_out, addr2);
  not not_19 (not_19_out, addr3);
  not not_20 (not_20_out, addr4);
  not not_21 (not_21_out, addr2);
  not not_22 (not_22_out, addr3);
  not not_23 (not_23_out, addr2);
  not not_24 (not_24_out, addr4);
  not not_25 (not_25_out, addr2);
  not not_26 (not_26_out, addr3);
  not not_27 (not_27_out, addr4);
  not not_28 (not_28_out, addr3);
  not not_29 (not_29_out, addr4);
  and two (two_out, not_1_out, addr2, addr3, addr4);
  and three (three_out, not_2_out, addr2, not_3_out, addr3);
  and four (four_out, not_4_out, addr2, not_5_out, addr4);
  and six (six_out, not_6_out, not_7_out, not_8_out, not_9_out);
  and seven (seven_out, not_10_out, not_11_out, not_12_out, addr4);
  and eight (eight_out, not_13_out, not_14_out, addr3, not_15_out);
  and nine (nine_out, not_16_out, not_17_out, addr3, addr4);
  and ten (ten_out, addr1, not_18_out, not_19_out, not_20_out);
  and eleven (eleven_out, addr1, not_21_out, not_22_out, addr4);
  and twelve (twelve_out, addr1, not_23_out, addr3, not_24_out);
  and thirdteen (thirdteen_out, addr1, not_25_out, addr3, addr4);
  and fourteen (fourteen_out, addr1, addr2, not_26_out, not_27_out);
  and fifteen (fifteen_out, addr1, addr2, not_28_out, addr4);
  and sixteen (sixteen_out, addr1, addr2, addr3, not_29_out);
  not not_30 (not_30_out, s_r_ff_10_q);
  not not_31 (not_31_out, s_r_ff_9_q);
  not not_32 (not_32_out, s_r_ff_11_q);
  not not_33 (not_33_out, s_r_ff_12_q);
  not not_34 (not_34_out, s_r_ff_16_q);
  not not_35 (not_35_out, s_r_ff_15_q);
  not not_36 (not_36_out, s_r_ff_14_q);
  not not_37 (not_37_out, s_r_ff_13_q);
  and and_1 (and_1_out, readwrite, s_r_ff_16_q, one_out);
  and and_2 (and_2_out, readwrite, s_r_ff_15_q, one_out);
  and and_3 (and_3_out, readwrite, s_r_ff_14_q, one_out);
  and and_4 (and_4_out, one_out, not_36_out, readwrite);
  and and_5 (and_5_out, one_out, not_37_out, readwrite);
  and and_6 (and_6_out, readwrite, s_r_ff_12_q, one_out);
  and and_7 (and_7_out, readwrite, s_r_ff_11_q, one_out);
  and and_8 (and_8_out, readwrite, s_r_ff_10_q, one_out);
  and and_9 (and_9_out, one_out, not_30_out, readwrite);
  and and_10 (and_10_out, one_out, not_31_out, readwrite);
  not not_38 (not_38_out, addr1);
  not not_39 (not_39_out, addr3);
  not not_40 (not_40_out, addr4);
  not not_41 (not_41_out, readwrite);
  not not_42 (not_42_out, readwrite);
  not not_43 (not_43_out, readwrite);
  not not_44 (not_44_out, readwrite);
  not not_45 (not_45_out, readwrite);
  not not_46 (not_46_out, readwrite);
  not not_47 (not_47_out, readwrite);
  not not_48 (not_48_out, readwrite);
  and and_11 (and_11_out, one_out, not_34_out, readwrite);
  and and_12 (and_12_out, one_out, not_35_out, readwrite);
  and and_13 (and_13_out, readwrite, s_r_ff_13_q, one_out);
  and and_14 (and_14_out, one_out, not_33_out, readwrite);
  and and_15 (and_15_out, one_out, not_32_out, readwrite);
  and and_16 (and_16_out, readwrite, s_r_ff_9_q, one_out);
  not not_49 (not_49_out, readwrite);
  S_R_Flip_Flop s_r_ff_1 (.clk(clk), .Q(s_r_ff_1_q), .reset(and_11_out), .preset(and_1_out));  // open: S, R, Qn
  S_R_Flip_Flop s_r_ff_2 (.clk(clk), .Q(s_r_ff_2_q), .reset(and_12_out), .preset(and_2_out));  // open: S, R, Qn
  S_R_Flip_Flop s_r_ff_3 (.clk(clk), .Q(s_r_ff_3_q), .reset(and_4_out), .preset(and_3_out));  // open: S, R, Qn
  S_R_Flip_Flop s_r_ff_4 (.clk(clk), .Q(s_r_ff_4_q), .reset(and_5_out), .preset(and_13_out));  // open: S, R, Qn
  S_R_Flip_Flop s_r_ff_5 (.clk(clk), .Q(s_r_ff_5_q), .reset(and_14_out), .preset(and_6_out));  // open: S, R, Qn
  S_R_Flip_Flop s_r_ff_6 (.clk(clk), .Q(s_r_ff_6_q), .reset(and_15_out), .preset(and_7_out));  // open: S, R, Qn
  S_R_Flip_Flop s_r_ff_7 (.clk(clk), .Q(s_r_ff_7_q), .reset(and_9_out), .preset(and_8_out));  // open: S, R, Qn
  S_R_Flip_Flop s_r_ff_8 (.clk(clk), .Q(s_r_ff_8_q), .reset(and_10_out), .preset(and_16_out));  // open: S, R, Qn
  and five (five_out, not_38_out, addr2, not_39_out, not_40_out);
  one_byte ppppp (
    .addr(two_out), .one(s_r_ff_16_q), .two(s_r_ff_15_q), .three(s_r_ff_14_q), .four(s_r_ff_13_q),
    .readwrite(readwrite), .clock(clk), .eight(s_r_ff_9_q), .seven(s_r_ff_10_q), .six(s_r_ff_11_q),
    .five(s_r_ff_12_q), .outone(ppppp_outone), .outtwo(ppppp_outtwo), .outthree(ppppp_outthree),
    .outfour(ppppp_outfour), .outfive(ppppp_outfive), .outsix(ppppp_outsix), .outseven(ppppp_outseven),
    .outeight(ppppp_outeight));
  one_byte one_byte_1 (
    .addr(three_out), .one(s_r_ff_16_q), .two(s_r_ff_15_q), .three(s_r_ff_14_q), .four(s_r_ff_13_q),
    .readwrite(readwrite), .clock(clk), .eight(s_r_ff_9_q), .seven(s_r_ff_10_q), .six(s_r_ff_11_q),
    .five(s_r_ff_12_q), .outone(one_byte_1_outone), .outtwo(one_byte_1_outtwo),
    .outthree(one_byte_1_outthree), .outfour(one_byte_1_outfour), .outfive(one_byte_1_outfive),
    .outsix(one_byte_1_outsix), .outseven(one_byte_1_outseven), .outeight(one_byte_1_outeight));
  one_byte one_byte_2 (
    .addr(four_out), .one(s_r_ff_16_q), .two(s_r_ff_15_q), .three(s_r_ff_14_q), .four(s_r_ff_13_q),
    .readwrite(readwrite), .clock(clk), .eight(s_r_ff_9_q), .seven(s_r_ff_10_q), .six(s_r_ff_11_q),
    .five(s_r_ff_12_q), .outone(one_byte_2_outone), .outtwo(one_byte_2_outtwo),
    .outthree(one_byte_2_outthree), .outfour(one_byte_2_outfour), .outfive(one_byte_2_outfive),
    .outsix(one_byte_2_outsix), .outseven(one_byte_2_outseven), .outeight(one_byte_2_outeight));
  and and_17 (and_17_out, readwrite, in8);
  and and_18 (and_18_out, not_41_out, out8);
  and and_19 (and_19_out, readwrite, in7);
  and and_20 (and_20_out, not_42_out, out7);
  and and_21 (and_21_out, readwrite, in6);
  and and_22 (and_22_out, not_43_out, out6);
  and and_23 (and_23_out, readwrite, in5);
  and and_24 (and_24_out, not_44_out, out5);
  and and_25 (and_25_out, readwrite, in4);
  and and_26 (and_26_out, not_45_out, out4);
  and and_27 (and_27_out, readwrite, in3);
  and and_28 (and_28_out, not_46_out, out3);
  and and_29 (and_29_out, readwrite, in2);
  and and_30 (and_30_out, not_47_out, out2);
  and and_31 (and_31_out, readwrite, in1);
  and and_32 (and_32_out, not_48_out, out1);
  or or_1 (or_1_out, and_17_out, and_18_out);
  or or_2 (or_2_out, and_19_out, and_20_out);
  or or_3 (or_3_out, and_21_out, and_22_out);
  or or_4 (or_4_out, and_23_out, and_24_out);
  or or_5 (or_5_out, and_25_out, and_26_out);
  or or_6 (or_6_out, and_27_out, and_28_out);
  or or_7 (or_7_out, and_29_out, and_30_out);
  or or_8 (or_8_out, and_31_out, and_32_out);
  and and_33 (and_33_out, s_r_ff_2_q, not_49_out, clk, one_out);
  and and_34 (and_34_out, s_r_ff_3_q, not_49_out, clk, one_out);
  and and_35 (and_35_out, one_out, s_r_ff_4_q, not_49_out, clk);
  and and_36 (and_36_out, s_r_ff_6_q, not_49_out, clk, one_out);
  and and_37 (and_37_out, s_r_ff_7_q, not_49_out, clk, one_out);
  and and_38 (and_38_out, one_out, s_r_ff_8_q, not_49_out, clk);
  not not_50 (not_50_out, or_1_out);
  not not_51 (not_51_out, or_2_out);
  not not_52 (not_52_out, or_3_out);
  not not_53 (not_53_out, or_4_out);
  not not_54 (not_54_out, or_5_out);
  not not_55 (not_55_out, or_6_out);
  not not_56 (not_56_out, or_7_out);
  not not_57 (not_57_out, or_8_out);
  and and_39 (and_39_out, s_r_ff_1_q, not_49_out, clk, one_out);
  and and_40 (and_40_out, s_r_ff_5_q, not_49_out, clk, one_out);
  S_R_Flip_Flop s_r_ff_9 (.clk(1'b1), .Q(s_r_ff_9_q), .reset(not_50_out), .preset(or_1_out));  // open: S, R, Qn
  S_R_Flip_Flop s_r_ff_10 (.clk(1'b1), .Q(s_r_ff_10_q), .reset(not_51_out), .preset(or_2_out));  // open: S, R, Qn
  S_R_Flip_Flop s_r_ff_11 (
    .R(undriven), .clk(1'b1), .Q(s_r_ff_11_q), .reset(not_52_out), .preset(or_3_out));  // open: S, Qn
  S_R_Flip_Flop s_r_ff_12 (
    .R(undriven_2), .clk(1'b1), .Q(s_r_ff_12_q), .reset(not_53_out), .preset(or_4_out));  // open: S, Qn
  S_R_Flip_Flop s_r_ff_13 (.clk(1'b1), .Q(s_r_ff_13_q), .reset(not_54_out), .preset(or_5_out));  // open: S, R, Qn
  S_R_Flip_Flop s_r_ff_14 (.clk(1'b1), .Q(s_r_ff_14_q), .reset(not_55_out), .preset(or_6_out));  // open: S, R, Qn
  S_R_Flip_Flop s_r_ff_15 (
    .R(undriven_3), .clk(1'b1), .Q(s_r_ff_15_q), .reset(not_56_out), .preset(or_7_out));  // open: S, Qn
  S_R_Flip_Flop s_r_ff_16 (
    .R(undriven_4), .clk(1'b1), .Q(s_r_ff_16_q), .reset(not_57_out), .preset(or_8_out));  // open: S, Qn
  one_byte a0010 (
    .addr(five_out), .one(s_r_ff_16_q), .two(s_r_ff_15_q), .three(s_r_ff_14_q), .four(s_r_ff_13_q),
    .readwrite(readwrite), .clock(clk), .eight(s_r_ff_9_q), .seven(s_r_ff_10_q), .six(s_r_ff_11_q),
    .five(s_r_ff_12_q), .outone(a0010_outone), .outtwo(a0010_outtwo), .outthree(a0010_outthree),
    .outfour(a0010_outfour), .outfive(a0010_outfive), .outsix(a0010_outsix), .outseven(a0010_outseven),
    .outeight(a0010_outeight));
  one_byte a0000 (
    .addr(six_out), .one(s_r_ff_16_q), .two(s_r_ff_15_q), .three(s_r_ff_14_q), .four(s_r_ff_13_q),
    .readwrite(readwrite), .clock(clk), .eight(s_r_ff_9_q), .seven(s_r_ff_10_q), .six(s_r_ff_11_q),
    .five(s_r_ff_12_q), .outone(a0000_outone), .outtwo(a0000_outtwo), .outthree(a0000_outthree),
    .outfour(a0000_outfour), .outfive(a0000_outfive), .outsix(a0000_outsix), .outseven(a0000_outseven),
    .outeight(a0000_outeight));
  one_byte one_byte_3 (
    .addr(seven_out), .one(s_r_ff_16_q), .two(s_r_ff_15_q), .three(s_r_ff_14_q), .four(s_r_ff_13_q),
    .readwrite(readwrite), .clock(clk), .eight(s_r_ff_9_q), .seven(s_r_ff_10_q), .six(s_r_ff_11_q),
    .five(s_r_ff_12_q), .outone(one_byte_3_outone), .outtwo(one_byte_3_outtwo),
    .outthree(one_byte_3_outthree), .outfour(one_byte_3_outfour), .outfive(one_byte_3_outfive),
    .outsix(one_byte_3_outsix), .outseven(one_byte_3_outseven), .outeight(one_byte_3_outeight));
  one_byte one_byte_4 (
    .addr(eight_out), .one(s_r_ff_16_q), .two(s_r_ff_15_q), .three(s_r_ff_14_q), .four(s_r_ff_13_q),
    .readwrite(readwrite), .clock(clk), .eight(s_r_ff_9_q), .seven(s_r_ff_10_q), .six(s_r_ff_11_q),
    .five(s_r_ff_12_q), .outone(one_byte_4_outone), .outtwo(one_byte_4_outtwo),
    .outthree(one_byte_4_outthree), .outfour(one_byte_4_outfour), .outfive(one_byte_4_outfive),
    .outsix(one_byte_4_outsix), .outseven(one_byte_4_outseven), .outeight(one_byte_4_outeight));
  one_byte one_byte_5 (
    .addr(nine_out), .one(s_r_ff_16_q), .two(s_r_ff_15_q), .three(s_r_ff_14_q), .four(s_r_ff_13_q),
    .readwrite(readwrite), .clock(clk), .eight(s_r_ff_9_q), .seven(s_r_ff_10_q), .six(s_r_ff_11_q),
    .five(s_r_ff_12_q), .outone(one_byte_4_outsix), .outtwo(one_byte_5_outtwo),
    .outthree(one_byte_5_outthree), .outfour(one_byte_5_outfour), .outfive(one_byte_5_outfive),
    .outsix(one_byte_5_outsix), .outseven(one_byte_5_outseven), .outeight(one_byte_5_outeight));
  one_byte a0001 (
    .addr(ten_out), .one(s_r_ff_16_q), .two(s_r_ff_15_q), .three(s_r_ff_14_q), .four(s_r_ff_13_q),
    .readwrite(readwrite), .clock(clk), .eight(s_r_ff_9_q), .seven(s_r_ff_10_q), .six(s_r_ff_11_q),
    .five(s_r_ff_12_q), .outone(a0001_outone), .outtwo(a0001_outtwo), .outthree(a0001_outthree),
    .outfour(a0001_outfour), .outfive(a0001_outfive), .outsix(a0001_outsix), .outseven(a0001_outseven),
    .outeight(a0001_outeight));
  one_byte one_byte_6 (
    .addr(sixteen_out), .one(s_r_ff_16_q), .two(s_r_ff_15_q), .three(s_r_ff_14_q), .four(s_r_ff_13_q),
    .readwrite(readwrite), .clock(clk), .eight(s_r_ff_9_q), .seven(s_r_ff_10_q), .six(s_r_ff_11_q),
    .five(s_r_ff_12_q), .outone(one_byte_6_outone), .outtwo(one_byte_6_outtwo),
    .outthree(one_byte_6_outthree), .outfour(one_byte_6_outfour), .outfive(one_byte_6_outfive),
    .outsix(one_byte_6_outsix), .outseven(one_byte_6_outseven), .outeight(one_byte_6_outeight));
  one_byte one_byte_7 (
    .addr(eleven_out), .one(s_r_ff_16_q), .two(s_r_ff_15_q), .three(s_r_ff_14_q), .four(s_r_ff_13_q),
    .readwrite(readwrite), .clock(clk), .eight(s_r_ff_9_q), .seven(s_r_ff_10_q), .six(s_r_ff_11_q),
    .five(s_r_ff_12_q), .outone(one_byte_7_outone), .outtwo(one_byte_7_outtwo),
    .outthree(one_byte_7_outthree), .outfour(one_byte_7_outfour), .outfive(one_byte_7_outfive),
    .outseven(one_byte_7_outseven), .outeight(one_byte_7_outeight));  // open: outsix
  one_byte one_byte_8 (
    .addr(twelve_out), .one(s_r_ff_16_q), .two(s_r_ff_15_q), .three(s_r_ff_14_q), .four(s_r_ff_13_q),
    .readwrite(readwrite), .clock(clk), .eight(s_r_ff_9_q), .seven(s_r_ff_10_q), .six(s_r_ff_11_q),
    .five(s_r_ff_12_q), .outone(one_byte_8_outone), .outtwo(one_byte_8_outtwo),
    .outthree(one_byte_8_outthree), .outfour(one_byte_8_outfour), .outfive(one_byte_8_outfive),
    .outsix(one_byte_8_outsix), .outseven(one_byte_8_outseven), .outeight(one_byte_8_outeight));
  one_byte one_byte_9 (
    .addr(thirdteen_out), .one(s_r_ff_16_q), .two(s_r_ff_15_q), .three(s_r_ff_14_q), .four(s_r_ff_13_q),
    .readwrite(readwrite), .clock(clk), .eight(s_r_ff_9_q), .seven(s_r_ff_10_q), .six(s_r_ff_11_q),
    .five(s_r_ff_12_q), .outone(one_byte_9_outone), .outtwo(one_byte_9_outtwo),
    .outthree(one_byte_9_outthree), .outfour(one_byte_9_outfour), .outfive(one_byte_9_outfive),
    .outsix(one_byte_9_outsix), .outseven(one_byte_9_outseven), .outeight(one_byte_9_outeight));
  one_byte one_byte_10 (
    .addr(fourteen_out), .one(s_r_ff_16_q), .two(s_r_ff_15_q), .three(s_r_ff_14_q), .four(s_r_ff_13_q),
    .readwrite(readwrite), .clock(clk), .eight(s_r_ff_9_q), .seven(s_r_ff_10_q), .six(s_r_ff_11_q),
    .five(s_r_ff_12_q), .outone(one_byte_10_outone), .outtwo(one_byte_10_outtwo),
    .outthree(one_byte_10_outthree), .outfour(one_byte_10_outfour), .outfive(one_byte_10_outfive),
    .outsix(one_byte_10_outsix), .outseven(one_byte_10_outseven), .outeight(one_byte_10_outeight));
  one_byte one_byte_11 (
    .addr(fifteen_out), .one(s_r_ff_16_q), .two(s_r_ff_15_q), .three(s_r_ff_14_q), .four(s_r_ff_13_q),
    .readwrite(readwrite), .clock(clk), .eight(s_r_ff_9_q), .seven(s_r_ff_10_q), .six(s_r_ff_11_q),
    .five(s_r_ff_12_q), .outone(one_byte_11_outone), .outtwo(one_byte_11_outtwo),
    .outthree(one_byte_11_outthree), .outfour(one_byte_11_outfour), .outfive(one_byte_11_outfive),
    .outsix(one_byte_11_outsix), .outseven(one_byte_11_outseven), .outeight(one_byte_11_outeight));
  or or_9 (out1, one_byte_11_outone, one_byte_3_outone, a0000_outone, a0010_outone, and_39_out, ppppp_outone, one_byte_1_outone, one_byte_2_outone, one_byte_4_outone, one_byte_4_outsix, a0001_outone, one_byte_6_outone, one_byte_7_outone, one_byte_8_outone, one_byte_9_outone, one_byte_10_outone);
  or or_10 (out2, and_33_out, a0010_outtwo, a0000_outtwo, one_byte_3_outtwo, one_byte_4_outtwo, one_byte_5_outtwo, a0001_outtwo, one_byte_6_outtwo, one_byte_7_outtwo, one_byte_8_outtwo, one_byte_9_outtwo, one_byte_10_outtwo, one_byte_11_outtwo, ppppp_outtwo, one_byte_1_outtwo, one_byte_2_outtwo);
  or or_11 (out3, one_byte_7_outthree, one_byte_8_outthree, one_byte_10_outthree, one_byte_11_outthree, and_34_out, one_byte_2_outthree, one_byte_4_outthree, one_byte_5_outthree, a0001_outthree, one_byte_6_outthree, a0010_outthree, a0000_outthree, one_byte_3_outthree, ppppp_outthree, one_byte_1_outthree, one_byte_9_outthree);
  or or_12 (out4, one_byte_7_outfour, one_byte_8_outfour, one_byte_9_outfour, one_byte_10_outfour, one_byte_11_outfour, one_byte_4_outfour, one_byte_5_outfour, a0001_outfour, one_byte_6_outfour, and_35_out, a0010_outfour, a0000_outfour, one_byte_3_outfour, ppppp_outfour, one_byte_1_outfour, one_byte_2_outfour);
  or or_13 (out5, one_byte_7_outfive, one_byte_8_outfive, one_byte_9_outfive, one_byte_10_outfive, one_byte_11_outfive, one_byte_4_outfive, one_byte_5_outfive, a0001_outfive, one_byte_6_outfive, a0010_outfive, a0000_outfive, one_byte_3_outfive, and_40_out, ppppp_outfive, one_byte_1_outfive, one_byte_2_outfive);
  or or_14 (out6, one_byte_8_outone, one_byte_8_outsix, one_byte_9_outsix, one_byte_11_outsix, one_byte_4_outsix, one_byte_5_outsix, a0001_outsix, one_byte_6_outsix, a0010_outsix, a0000_outsix, one_byte_3_outsix, and_36_out, ppppp_outsix, one_byte_1_outsix, one_byte_2_outsix, one_byte_10_outsix);
  or or_15 (out7, one_byte_7_outseven, one_byte_8_outseven, one_byte_9_outseven, one_byte_10_outseven, one_byte_11_outseven, one_byte_4_outseven, one_byte_5_outseven, a0001_outseven, one_byte_6_outseven, a0010_outseven, a0000_outseven, one_byte_3_outseven, ppppp_outseven, one_byte_1_outseven, one_byte_2_outseven, and_37_out);
  or or_16 (out8, one_byte_7_outeight, one_byte_8_outeight, one_byte_9_outeight, one_byte_10_outeight, one_byte_11_outeight, one_byte_4_outeight, one_byte_5_outeight, a0001_outeight, one_byte_6_outeight, one_byte_3_outeight, a0000_outeight, a0010_outeight, ppppp_outeight, one_byte_1_outeight, one_byte_2_outeight, and_38_out);

  // Notes on the sheet:
  //   4
  //   2
  //   3
  //   1
  //   address register
  //   read/write
  //   clock
  //   cpu clock
  //   cpu clock
  //   data register
  //   data register
endmodule

module one_byte (
  input  addr,
  input  one,
  input  two,
  input  three,
  input  four,
  input  readwrite,
  input  clock,
  input  eight,
  input  seven,
  input  six,
  input  five,
  output outone,
  output outtwo,
  output outthree,
  output outfour,
  output outfive,
  output outsix,
  output outseven,
  output outeight
);

  wire and_1_out, and_2_out, and_3_out, and_4_out, and_5_out, and_6_out, and_7_out, and_8_out, and_9_out,
       and_10_out, and_11_out, and_12_out, and_13_out, and_14_out, and_15_out, and_16_out, not_1_out,
       not_2_out, not_3_out, not_4_out, not_5_out, not_6_out, not_7_out, not_8_out, not_9_out, s_r_ff_1_q,
       s_r_ff_2_q, s_r_ff_3_q, s_r_ff_4_q, s_r_ff_5_q, s_r_ff_6_q, s_r_ff_7_q, s_r_ff_8_q;

  not not_1 (not_1_out, seven);
  not not_2 (not_2_out, eight);
  not not_3 (not_3_out, six);
  not not_4 (not_4_out, five);
  not not_5 (not_5_out, one);
  not not_6 (not_6_out, two);
  not not_7 (not_7_out, three);
  not not_8 (not_8_out, four);
  and and_1 (and_1_out, readwrite, one, addr);
  and and_2 (and_2_out, readwrite, two, addr);
  and and_3 (and_3_out, readwrite, three, addr);
  and and_4 (and_4_out, addr, not_7_out, readwrite);
  and and_5 (and_5_out, addr, not_8_out, readwrite);
  and and_6 (and_6_out, readwrite, five, addr);
  and and_7 (and_7_out, readwrite, six, addr);
  and and_8 (and_8_out, readwrite, seven, addr);
  and and_9 (and_9_out, addr, not_1_out, readwrite);
  and and_10 (and_10_out, addr, not_2_out, readwrite);
  and and_11 (and_11_out, addr, not_5_out, readwrite);
  and and_12 (and_12_out, addr, not_6_out, readwrite);
  and and_13 (and_13_out, readwrite, four, addr);
  and and_14 (and_14_out, addr, not_4_out, readwrite);
  and and_15 (and_15_out, addr, not_3_out, readwrite);
  and and_16 (and_16_out, readwrite, eight, addr);
  not not_9 (not_9_out, readwrite);
  S_R_Flip_Flop s_r_ff_1 (.clk(clock), .Q(s_r_ff_1_q), .reset(and_11_out), .preset(and_1_out));  // open: S, R, Qn
  S_R_Flip_Flop s_r_ff_2 (.clk(clock), .Q(s_r_ff_2_q), .reset(and_12_out), .preset(and_2_out));  // open: S, R, Qn
  S_R_Flip_Flop s_r_ff_3 (.clk(clock), .Q(s_r_ff_3_q), .reset(and_4_out), .preset(and_3_out));  // open: S, R, Qn
  S_R_Flip_Flop s_r_ff_4 (.clk(clock), .Q(s_r_ff_4_q), .reset(and_5_out), .preset(and_13_out));  // open: S, R, Qn
  S_R_Flip_Flop s_r_ff_5 (.clk(clock), .Q(s_r_ff_5_q), .reset(and_14_out), .preset(and_6_out));  // open: S, R, Qn
  S_R_Flip_Flop s_r_ff_6 (.clk(clock), .Q(s_r_ff_6_q), .reset(and_15_out), .preset(and_7_out));  // open: S, R, Qn
  S_R_Flip_Flop s_r_ff_7 (.clk(clock), .Q(s_r_ff_7_q), .reset(and_9_out), .preset(and_8_out));  // open: S, R, Qn
  S_R_Flip_Flop s_r_ff_8 (.clk(clock), .Q(s_r_ff_8_q), .reset(and_10_out), .preset(and_16_out));  // open: S, R, Qn
  and and_17 (outtwo, s_r_ff_2_q, not_9_out, clock, addr);
  and and_18 (outthree, s_r_ff_3_q, not_9_out, clock, addr);
  and and_19 (outfour, addr, s_r_ff_4_q, not_9_out, clock);
  and and_20 (outsix, s_r_ff_6_q, not_9_out, clock, addr);
  and and_21 (outseven, s_r_ff_7_q, not_9_out, clock, addr);
  and and_22 (outeight, addr, s_r_ff_8_q, not_9_out, clock);
  and and_23 (outone, s_r_ff_1_q, not_9_out, clock, addr);
  and and_24 (outfive, s_r_ff_5_q, not_9_out, clock, addr);

  // Notes on the sheet:
  //   5
  //   addr
endmodule

module cpu (
  input  in_1,
  input  in_2,
  input  in_3,
  input  in_4,
  input  in_5,
  input  in_6,
  input  in_7,
  input  in_8,
  input  [7:0] in_9,
  input  in_10,
  input  in_11,
  input  _5,
  input  in_13,
  input  in_14,
  input  [9:0] in_15,
  input  in_16,
  input  in_17,
  input  in_18,
  input  in_19,
  input  [7:0] in_20,
  input  in_21,
  input  [7:0] in_22,
  input  in_23,
  output [7:0] out_24,
  output [7:0] out_25,
  output [7:0] out_26,
  output [7:0] out_27,
  output [2:0] status_register,
  output [7:0] out_29,
  output [7:0] out_30,
  output [2:0] out_31
);

  wire and_1_out, and_2_out, and_3_out, and_4_out, and_5_out, and_6_out, and_7_out, and_8_out, and_9_out,
       and_10_out, and_11_out, and_12_out, and_13_out, and_14_out, and_15_out, and_16_out, and_17_out,
       and_18_out, and_19_out, AR_oone, AR_othree, AR_otwo, AR_pfour, cu_1_eight, cu_1_fifteen, cu_1_five,
       cu_1_four, cu_1_nine, cu_1_ofive, cu_1_ofour, cu_1_one, cu_1_oone, cu_1_oseven, cu_1_osix,
       cu_1_othree, cu_1_otwo, cu_1_ozero, cu_1_seven, cu_1_six, cu_1_three, cu_1_two, cu_1_zero,
       display_connect_to_main_1_out_11, display_connect_to_main_1_out_12, display_connect_to_main_1_out_13,
       display_connect_to_main_1_out_14, display_connect_to_main_1_out_15, display_connect_to_main_1_out_16,
       display_connect_to_main_1_out_17, display_connect_to_main_1_out_18, display_connect_to_main_1_out_19,
       display_connect_to_main_1_out_20, display_connect_to_main_1_out_21, display_connect_to_main_1_out_22,
       display_connect_to_main_1_out_23, display_connect_to_main_1_out_24, display_connect_to_main_1_out_25,
       display_connect_to_main_1_out_26, display_connect_to_main_1_out_27, display_connect_to_main_1_out_28,
       display_connect_to_main_1_out_29, display_connect_to_main_1_out_30, display_connect_to_main_1_out_31,
       eight0_out, five0_out, five1_out, FIVE4ADD_out, four0_out, four1_out, gate8bits_1_o1, gate8bits_1_o2,
       gate8bits_1_o3, gate8bits_1_o4, gate8bits_1_o5, gate8bits_1_o6, gate8bits_1_o7, gate8bits_1_o8,
       gate8bits_2_o1, gate8bits_2_o2, gate8bits_2_o3, gate8bits_2_o4, gate8bits_2_o5, gate8bits_2_o6,
       gate8bits_2_o7, gate8bits_2_o8, gate_1_ofour, gate_1_oone, gate_1_othree, gate_1_otwo, inc_1_ofour,
       inc_1_oone, inc_1_othree, inc_1_otwo, inc_2_ofour, inc_2_oone, inc_2_othree, inc_2_otwo, main_1_out1,
       main_1_out2, main_1_out3, main_1_out4, main_1_out5, main_1_out6, main_1_out7, main_1_out8, MAR_oone,
       MAR_othree, MAR_otwo, MAR_pfour, mbr_1_oeight, mbr_1_ofive, mbr_1_ofour, mbr_1_oone, mbr_1_oseven,
       mbr_1_osix, mbr_1_othree, mbr_1_otwo, mbr_2_oeight, mbr_2_ofive, mbr_2_ofour, mbr_2_oone,
       mbr_2_oseven, mbr_2_osix, mbr_2_othree, mbr_2_otwo, mbr_3_ofour, mbrtoir_1_out_10, mbrtoir_1_out_11,
       mbrtoir_1_out_12, mbrtoir_1_out_13, mbrtoir_1_out_14, mbrtoir_1_out_15, mbrtoir_1_out_16,
       mbrtoir_1_out_17, multiplexer_2_out, multiplexer_3_out, multiplexer_4_out, multiplexer_5_out,
       multiplexer_6_out, multiplexer_7_out, multiplexer_8_out, multiplexer_9_out, multiplexer_10_out,
       multiplexer_11_out, multiplexer_12_out, multiplexer_13_out, multiplexer_14_out, multiplexer_15_out,
       multiplexer_16_out, multiplexer_17_out, multiplexer_18_out, muuuuux_1_out1, muuuuux_1_out2,
       muuuuux_1_out3, muuuuux_1_out4, muuuuux_1_out5, muuuuux_1_out6, muuuuux_1_out7, muuuuux_1_out8,
       nine0_out, not_1_out, not_2_out, not_3_out, not_4_out, not_5_out, not_6_out, not_7_out, not_8_out,
       not_9_out, not_10_out, not_11_out, not_12_out, not_13_out, not_14_out, not_15_out, not_16_out,
       not_17_out, not_18_out, not_19_out, not_21_out, not_22_out, not_23_out, not_24_out, not_25_out,
       not_26_out, not_27_out, not_28_out, not_29_out, not_30_out, not_31_out, not_32_out, not_33_out,
       not_34_out, not_35_out, one_byte_1_outeight, one_byte_1_outfive, one_byte_1_outfour,
       one_byte_1_outone, one_byte_1_outseven, one_byte_1_outsix, one_byte_1_outthree, one_byte_1_outtwo,
       onebitsecure_1_out_5, or_1_out, or_2_out, or_3_out, or_4_out, or_5_out, or_6_out, or_7_out, or_8_out,
       or_9_out, or_10_out, or_11_out, or_12_out, or_13_out, or_14_out, or_15_out, or_16_out, or_17_out,
       or_18_out, or_19_out, or_20_out, or_21_out, or_22_out, or_23_out, or_25_out, or_26_out, or_27_out,
       or_28_out, or_29_out, or_30_out, or_31_out, pc_1_ofour, pc_1_oone, pc_1_othree, pc_1_otwo, pc_2_ofour,
       pc_2_oone, pc_2_othree, pc_2_otwo, s_r_ff_1_q, s_r_ff_2_q, s_r_ff_3_q, seven0_out, seven4add_out,
       six0_out, SIX4ADD_out, tom_1_oone, tom_1_othree, tom_1_otwo, tom_1_pfour, tom_2_oone, tom_2_othree,
       tom_2_otwo, tom_2_pfour, tom_3_oone, tom_3_othree, tom_3_otwo, tom_3_pfour, tom_4_oone, tom_4_othree,
       tom_4_otwo, tom_4_pfour, xnor_1_out;
  wire [2:0] mbr_3_oone, or_24_out, ram3bit_1_out_5;
  wire [3:0] gate_2_oone, mbr_3_ofive, ram4bitssecure_1_out_5;
  wire [7:0] alunew_1_result, controlled_buffer_4_out, controlled_buffer_5_out, controlled_buffer_6_out,
       controlled_buffer_11_out, controlled_buffer_12_out, controlled_buffer_14_out,
       controlled_buffer_15_out, controlled_buffer_16_out, controlled_buffer_20_out, DR_oone, gate8bits_3_o1,
       gate8bits_4_o1, keybb_1_out_2, MBR1_oone, one_byte_2_outone, one_byte_evo_2_out_5,
       one_byte_evo_3_out_5, undriven;

  keybb keybb_1 (.in_1(in_15), .out_2(keybb_1_out_2));
  assign out_25 = and_18_out ? keybb_1_out_2 : 8'bz;  // Controlled_Buffer controlled_buffer_1
  _7_Segment_Display u_7_segment_display_1 (
    .g(display_connect_to_main_1_out_17), .f(display_connect_to_main_1_out_18),
    .a(display_connect_to_main_1_out_19), .b(display_connect_to_main_1_out_20),
    .e(display_connect_to_main_1_out_21), .d(display_connect_to_main_1_out_22),
    .c(display_connect_to_main_1_out_23));  // open: dp
  gate8bits gate8bits_1 (
    .d1(DR_oone[0]), .c2(eight0_out), .d2(DR_oone[1]), .d3(DR_oone[2]), .d4(DR_oone[3]), .d5(DR_oone[4]),
    .d6(DR_oone[5]), .d7(DR_oone[6]), .d8(DR_oone[7]), .o1(gate8bits_1_o1), .o2(gate8bits_1_o2),
    .o3(gate8bits_1_o3), .o4(gate8bits_1_o4), .o5(gate8bits_1_o5), .o6(gate8bits_1_o6), .o7(gate8bits_1_o7),
    .o8(gate8bits_1_o8));  // open: c1, c3, c4
  Display_Connect_to_Main display_connect_to_main_1 (
    .in_1(out_25[7]), .in_2(out_25[6]), .in_3(out_25[5]), .in_4(out_25[4]), .in_5(out_25[3]),
    .in_6(out_25[2]), .in_7(out_25[1]), .in_8(out_25[0]), .in_9(in_13),
    .out_17(display_connect_to_main_1_out_17), .out_18(display_connect_to_main_1_out_18),
    .out_19(display_connect_to_main_1_out_19), .out_20(display_connect_to_main_1_out_20),
    .out_21(display_connect_to_main_1_out_21), .out_22(display_connect_to_main_1_out_22),
    .out_23(display_connect_to_main_1_out_23), .out_25(display_connect_to_main_1_out_25),
    .out_26(display_connect_to_main_1_out_26), .out_27(display_connect_to_main_1_out_27),
    .out_28(display_connect_to_main_1_out_28), .out_29(display_connect_to_main_1_out_29),
    .out_30(display_connect_to_main_1_out_30), .out_31(display_connect_to_main_1_out_31),
    .out_11(display_connect_to_main_1_out_11), .out_12(display_connect_to_main_1_out_12),
    .out_13(display_connect_to_main_1_out_13), .out_14(display_connect_to_main_1_out_14),
    .out_15(display_connect_to_main_1_out_15), .out_16(display_connect_to_main_1_out_16),
    .out_24(display_connect_to_main_1_out_24), .out_10(out_29));
  _7_Segment_Display u_7_segment_display_2 (
    .g(display_connect_to_main_1_out_25), .f(display_connect_to_main_1_out_26),
    .a(display_connect_to_main_1_out_27), .b(display_connect_to_main_1_out_28),
    .e(display_connect_to_main_1_out_29), .d(display_connect_to_main_1_out_30),
    .c(display_connect_to_main_1_out_31));  // open: dp
  assign out_25 = mbr_3_ofour ? controlled_buffer_12_out : 8'bz;  // Controlled_Buffer controlled_buffer_2
  _7_Segment_Display u_7_segment_display_3 (
    .g(display_connect_to_main_1_out_11), .f(display_connect_to_main_1_out_12),
    .a(display_connect_to_main_1_out_13), .b(display_connect_to_main_1_out_14),
    .e(display_connect_to_main_1_out_15), .d(display_connect_to_main_1_out_16),
    .c(display_connect_to_main_1_out_24));  // open: dp
  assign out_25 = not_1_out ? controlled_buffer_11_out : 8'bz;  // Controlled_Buffer controlled_buffer_3
  not not_1 (not_1_out, mbr_3_ofour);
  and and_1 (and_1_out, not_2_out, muuuuux_1_out3);
  not not_2 (not_2_out, cu_1_zero);
  assign controlled_buffer_4_out = mbr_3_ofour ? out_25 : 8'bz;  // Controlled_Buffer controlled_buffer_4
  assign controlled_buffer_5_out = not_1_out ? out_25 : 8'bz;  // Controlled_Buffer controlled_buffer_5
  assign controlled_buffer_6_out = and_13_out ? one_byte_evo_3_out_5 : 8'bz;  // Controlled_Buffer controlled_buffer_6
  or or_1 (or_1_out, and_13_out, mbr_3_ofour);
  assign controlled_buffer_6_out = five1_out ? DR_oone : 8'bz;  // Controlled_Buffer controlled_buffer_7
  or or_2 (or_2_out, and_18_out, and_13_out, FIVE4ADD_out, cu_1_othree);
  or or_3 (or_3_out, five1_out, and_18_out);
  muuuuux muuuuux_1 (
    .A1(main_1_out1), .B1(out_25[0]), .A2(main_1_out2), .B2(out_25[1]), .A3(main_1_out3), .B3(out_25[2]),
    .A4(main_1_out4), .B4(out_25[3]), .A5(main_1_out5), .B5(out_25[4]), .A6(main_1_out6), .B6(out_25[5]),
    .A7(main_1_out7), .B7(out_25[6]), .A8(main_1_out8), .B8(out_25[7]), .condition(seven0_out),
    .out1(muuuuux_1_out1), .out2(muuuuux_1_out2), .out3(muuuuux_1_out3), .out4(muuuuux_1_out4),
    .out5(muuuuux_1_out5), .out6(muuuuux_1_out6), .out7(muuuuux_1_out7), .out8(muuuuux_1_out8));
  gate8bits gate8bits_2 (
    .c1(cu_1_two), .d1(muuuuux_1_out1), .c2(seven0_out), .d2(muuuuux_1_out2), .c3(five1_out), .d3(and_1_out),
    .d4(muuuuux_1_out4), .d5(muuuuux_1_out5), .d6(muuuuux_1_out6), .d7(muuuuux_1_out7), .d8(muuuuux_1_out8),
    .o1(gate8bits_2_o1), .o2(gate8bits_2_o2), .o3(gate8bits_2_o3), .o4(gate8bits_2_o4), .o5(gate8bits_2_o5),
    .o6(gate8bits_2_o6), .o7(gate8bits_2_o7), .o8(gate8bits_2_o8));  // open: c4
  or or_4 (or_4_out, or_6_out, five1_out);
  mbr DR (
    .clk(or_4_out), .one(gate8bits_2_o1), .two(gate8bits_2_o2), .three(gate8bits_2_o3),
    .four(gate8bits_2_o4), .five(gate8bits_2_o5), .six(gate8bits_2_o6), .seven(gate8bits_2_o7),
    .eight(gate8bits_2_o8), .oone(DR_oone[0]), .otwo(DR_oone[1]), .othree(DR_oone[2]), .ofour(DR_oone[3]),
    .ofive(DR_oone[4]), .osix(DR_oone[5]), .oseven(DR_oone[6]), .oeight(DR_oone[7]));
  or or_5 (or_5_out, five1_out, and_18_out, and_13_out);
  gate gate_1 (
    .c1(cu_1_one), .d1(AR_oone), .c2(eight0_out), .d2(AR_otwo), .c3(cu_1_two), .d3(AR_othree),
    .c4(five1_out), .d4(AR_pfour), .oone(gate_1_oone), .otwo(gate_1_otwo), .othree(gate_1_othree),
    .ofour(gate_1_ofour));
  or or_6 (or_6_out, eight0_out, seven0_out, cu_1_zero, cu_1_three, cu_1_three);
  assign controlled_buffer_5_out = or_1_out ? controlled_buffer_6_out : 8'bz;  // Controlled_Buffer controlled_buffer_8
  assign controlled_buffer_4_out = not_6_out ? controlled_buffer_6_out : 8'bz;  // Controlled_Buffer controlled_buffer_9
  tom AR (
    .clk(xnor_1_out), .one(gate_2_oone[0]), .two(gate_2_oone[1]), .three(gate_2_oone[2]),
    .four(gate_2_oone[3]), .oone(AR_oone), .otwo(AR_otwo), .othree(AR_othree), .pfour(AR_pfour));
  or or_7 (or_7_out, five1_out, SIX4ADD_out, or_8_out);
  or or_8 (or_8_out, five0_out, and_18_out, cu_1_othree);
  main main_1 (
    .in8(gate8bits_1_o8), .in7(gate8bits_1_o7), .in6(gate8bits_1_o6), .in5(gate8bits_1_o5),
    .in4(gate8bits_1_o4), .in3(gate8bits_1_o3), .in2(gate8bits_1_o2), .in1(gate8bits_1_o1), .clk(1'b1),
    .readwrite(eight0_out), .addr1(gate_1_oone), .addr2(gate_1_otwo), .addr3(gate_1_othree),
    .addr4(gate_1_ofour), .out8(main_1_out8), .out7(main_1_out7), .out6(main_1_out6), .out5(main_1_out5),
    .out4(main_1_out4), .out3(main_1_out3), .out2(main_1_out2), .out1(main_1_out1));
  Multiplexer #(.enable("false")) multiplexer_1 (.in0(in_10), .in1(in_11), .sel(_5));  // open: out
  or or_9 (or_9_out, five0_out, or_2_out, five1_out);
  assign out_25 = seven0_out ? MBR1_oone : 8'bz;  // Controlled_Buffer controlled_buffer_10
  not not_3 (not_3_out, five0_out);
  assign controlled_buffer_11_out = and_2_out ? undriven : 8'bz;  // Controlled_Buffer controlled_buffer_11
  assign controlled_buffer_12_out = and_2_out ? one_byte_2_outone : 8'bz;  // Controlled_Buffer controlled_buffer_12
  not not_4 (not_4_out, cu_1_fifteen);
  and and_2 (and_2_out, cu_1_othree, cu_1_five);
  assign out_25 = cu_1_three ? DR_oone : 8'bz;  // Controlled_Buffer controlled_buffer_13
  and and_3 (and_3_out, not_4_out, not_3_out);
  one_byte one_byte_1 (
    .addr(1'b1), .one(controlled_buffer_5_out[0]), .two(controlled_buffer_5_out[1]),
    .three(controlled_buffer_5_out[2]), .four(controlled_buffer_5_out[3]), .readwrite(or_5_out),
    .clock(or_9_out), .eight(controlled_buffer_5_out[7]), .seven(controlled_buffer_5_out[6]),
    .six(controlled_buffer_5_out[5]), .five(controlled_buffer_5_out[4]), .outone(one_byte_1_outone),
    .outtwo(one_byte_1_outtwo), .outthree(one_byte_1_outthree), .outfour(one_byte_1_outfour),
    .outfive(one_byte_1_outfive), .outsix(one_byte_1_outsix), .outseven(one_byte_1_outseven),
    .outeight(one_byte_1_outeight));
  one_byte one_byte_2 (
    .addr(1'b1), .one(controlled_buffer_4_out[0]), .two(controlled_buffer_4_out[1]),
    .three(controlled_buffer_4_out[2]), .four(controlled_buffer_4_out[3]), .readwrite(or_3_out),
    .clock(or_7_out), .eight(controlled_buffer_4_out[7]), .seven(controlled_buffer_4_out[6]),
    .six(controlled_buffer_4_out[5]), .five(controlled_buffer_4_out[4]), .outone(one_byte_2_outone[0]),
    .outtwo(one_byte_2_outone[1]), .outthree(one_byte_2_outone[2]), .outfour(one_byte_2_outone[3]),
    .outfive(one_byte_2_outone[4]), .outsix(one_byte_2_outone[5]), .outseven(one_byte_2_outone[6]),
    .outeight(one_byte_2_outone[7]));
  mbr mbr_1 (
    .clk(and_3_out), .one(one_byte_1_outone), .two(one_byte_1_outtwo), .three(one_byte_1_outthree),
    .four(one_byte_1_outfour), .five(one_byte_1_outfive), .six(one_byte_1_outsix),
    .seven(one_byte_1_outseven), .eight(one_byte_1_outeight), .oone(mbr_1_oone), .otwo(mbr_1_otwo),
    .othree(mbr_1_othree), .ofour(mbr_1_ofour), .ofive(mbr_1_ofive), .osix(mbr_1_osix),
    .oseven(mbr_1_oseven), .oeight(mbr_1_oeight));
  mbr mbr_2 (
    .clk(and_3_out), .one(one_byte_2_outone[0]), .two(one_byte_2_outone[1]), .three(one_byte_2_outone[2]),
    .four(one_byte_2_outone[3]), .five(one_byte_2_outone[4]), .six(one_byte_2_outone[5]),
    .seven(one_byte_2_outone[6]), .eight(one_byte_2_outone[7]), .oone(mbr_2_oone), .otwo(mbr_2_otwo),
    .othree(mbr_2_othree), .ofour(mbr_2_ofour), .ofive(mbr_2_ofive), .osix(mbr_2_osix),
    .oseven(mbr_2_oseven), .oeight(mbr_2_oeight));
  not not_5 (not_5_out, or_10_out);
  and and_4 (and_4_out, out_25[0], or_10_out);
  and and_5 (and_5_out, out_25[1], or_10_out);
  and and_6 (and_6_out, out_25[2], or_10_out);
  and and_7 (and_7_out, out_25[3], or_10_out);
  and and_8 (and_8_out, out_25[4], or_10_out);
  and and_9 (and_9_out, out_25[5], or_10_out);
  and and_10 (and_10_out, out_25[6], or_10_out);
  and and_11 (and_11_out, out_25[7], or_10_out);
  NotExactlyOne xnor_1 (.out(xnor_1_out), .in0(or_21_out), .in1(nine0_out), .in2(cu_1_three));
  Multiplexer #(.enable("false")) multiplexer_2 (
    .in0(and_4_out), .in1(controlled_buffer_16_out[0]), .out(multiplexer_2_out), .sel(six0_out));
  Multiplexer #(.enable("false")) multiplexer_3 (
    .in0(and_5_out), .in1(controlled_buffer_16_out[1]), .out(multiplexer_3_out), .sel(six0_out));
  Multiplexer #(.enable("false")) multiplexer_4 (
    .in0(and_6_out), .in1(controlled_buffer_16_out[2]), .out(multiplexer_4_out), .sel(six0_out));
  Multiplexer #(.enable("false")) multiplexer_5 (
    .in0(and_7_out), .in1(controlled_buffer_16_out[3]), .out(multiplexer_5_out), .sel(six0_out));
  NotExactlyOne xnor_2 (.in0(in_4), .in1(in_5), .in2(in_6));  // open: out
  gate gate_2 (
    .c1(cu_1_zero), .d1(MAR_oone), .c2(or_21_out), .d2(MAR_otwo), .c3(five0_out), .d3(MAR_othree),
    .c4(six0_out), .d4(MAR_pfour), .oone(gate_2_oone[0]), .otwo(gate_2_oone[1]), .othree(gate_2_oone[2]),
    .ofour(gate_2_oone[3]));
  or or_10 (or_10_out, cu_1_three, six0_out);
  Multiplexer #(.enable("false")) multiplexer_6 (
    .in0(and_8_out), .in1(controlled_buffer_16_out[4]), .out(multiplexer_6_out), .sel(six0_out));
  Multiplexer #(.enable("false")) multiplexer_7 (
    .in0(and_9_out), .in1(controlled_buffer_16_out[5]), .out(multiplexer_7_out), .sel(six0_out));
  Multiplexer #(.enable("false")) multiplexer_8 (
    .in0(and_10_out), .in1(controlled_buffer_16_out[6]), .out(multiplexer_8_out), .sel(six0_out));
  gate8bits gate8bits_3 (
    .c1(six0_out), .d1(mbr_1_oone), .c2(FIVE4ADD_out), .d2(mbr_1_otwo), .d3(mbr_1_othree), .d4(mbr_1_ofour),
    .d5(mbr_1_ofive), .d6(mbr_1_osix), .d7(mbr_1_oseven), .d8(mbr_1_oeight), .o1(gate8bits_3_o1[0]),
    .o2(gate8bits_3_o1[1]), .o3(gate8bits_3_o1[2]), .o4(gate8bits_3_o1[3]), .o5(gate8bits_3_o1[4]),
    .o6(gate8bits_3_o1[5]), .o7(gate8bits_3_o1[6]), .o8(gate8bits_3_o1[7]));  // open: c3, c4
  gate8bits gate8bits_4 (
    .c1(six0_out), .d1(mbr_2_oone), .c2(SIX4ADD_out), .d2(mbr_2_otwo), .d3(mbr_2_othree), .d4(mbr_2_ofour),
    .d5(mbr_2_ofive), .d6(mbr_2_osix), .d7(mbr_2_oseven), .d8(mbr_2_oeight), .o1(gate8bits_4_o1[0]),
    .o2(gate8bits_4_o1[1]), .o3(gate8bits_4_o1[2]), .o4(gate8bits_4_o1[3]), .o5(gate8bits_4_o1[4]),
    .o6(gate8bits_4_o1[5]), .o7(gate8bits_4_o1[6]), .o8(gate8bits_4_o1[7]));  // open: c3, c4
  Multiplexer #(.enable("false")) multiplexer_9 (
    .in0(and_11_out), .in1(controlled_buffer_16_out[7]), .out(multiplexer_9_out), .sel(six0_out));
  Multiplexer #(.enable("false")) multiplexer_10 (.in0(in_1), .in1(in_2), .out(multiplexer_10_out), .sel(in_3));
  mbr MBR1 (
    .clk(not_5_out), .one(multiplexer_2_out), .two(multiplexer_3_out), .three(multiplexer_4_out),
    .four(multiplexer_5_out), .five(multiplexer_6_out), .six(multiplexer_7_out), .seven(multiplexer_8_out),
    .eight(multiplexer_9_out), .oone(MBR1_oone[0]), .otwo(MBR1_oone[1]), .othree(MBR1_oone[2]),
    .ofour(MBR1_oone[3]), .ofive(MBR1_oone[4]), .osix(MBR1_oone[5]), .oseven(MBR1_oone[6]),
    .oeight(MBR1_oone[7]));
  assign controlled_buffer_14_out = or_11_out ? gate8bits_3_o1 : 8'bz;  // Controlled_Buffer controlled_buffer_14
  or or_11 (or_11_out, FIVE4ADD_out, and_12_out);
  or or_12 (or_12_out, mbr_3_ofour, FIVE4ADD_out);
  assign controlled_buffer_15_out = or_14_out ? gate8bits_4_o1 : 8'bz;  // Controlled_Buffer controlled_buffer_15
  or or_13 (or_13_out, not_6_out, SIX4ADD_out);
  or or_14 (or_14_out, and_12_out, SIX4ADD_out);
  tom MAR (
    .clk(or_15_out), .one(multiplexer_11_out), .two(multiplexer_14_out), .three(multiplexer_17_out),
    .four(multiplexer_18_out), .oone(MAR_oone), .otwo(MAR_otwo), .othree(MAR_othree), .pfour(MAR_pfour));
  assign controlled_buffer_16_out = or_12_out ? controlled_buffer_14_out : 8'bz;  // Controlled_Buffer controlled_buffer_16
  assign controlled_buffer_16_out = or_13_out ? controlled_buffer_15_out : 8'bz;  // Controlled_Buffer controlled_buffer_17
  or or_15 (or_15_out, or_21_out, cu_1_zero);
  mbr mbr_3 (
    .clk(or_20_out), .one(mbrtoir_1_out_10), .two(mbrtoir_1_out_11), .three(mbrtoir_1_out_12),
    .four(mbrtoir_1_out_13), .five(mbrtoir_1_out_14), .six(mbrtoir_1_out_15), .seven(mbrtoir_1_out_16),
    .eight(mbrtoir_1_out_17), .oone(mbr_3_oone[0]), .otwo(mbr_3_oone[1]), .othree(mbr_3_oone[2]),
    .ofour(mbr_3_ofour), .ofive(mbr_3_ofive[0]), .osix(mbr_3_ofive[1]), .oseven(mbr_3_ofive[2]),
    .oeight(mbr_3_ofive[3]));
  MBRtoIR mbrtoir_1 (
    .one(MBR1_oone[0]), .in_2(MBR1_oone[1]), .in_3(MBR1_oone[2]), .in_4(MBR1_oone[3]), .in_5(MBR1_oone[4]),
    .in_6(MBR1_oone[5]), .in_7(MBR1_oone[6]), .in_8(MBR1_oone[7]), .in_9(cu_1_four),
    .out_10(mbrtoir_1_out_10), .out_11(mbrtoir_1_out_11), .out_12(mbrtoir_1_out_12),
    .out_13(mbrtoir_1_out_13), .out_14(mbrtoir_1_out_14), .out_15(mbrtoir_1_out_15),
    .out_16(mbrtoir_1_out_16), .out_17(mbrtoir_1_out_17));
  not not_6 (not_6_out, mbr_3_ofour);
  Multiplexer #(.enable("false")) multiplexer_11 (
    .in0(pc_1_oone), .in1(mbr_3_ofive[0]), .out(multiplexer_11_out), .sel(or_21_out));
  not not_7 (not_7_out, MBR1_oone[1]);
  not not_8 (not_8_out, MBR1_oone[2]);
  not not_9 (not_9_out, MBR1_oone[0]);
  and and_12 (and_12_out, not_8_out, not_9_out, not_7_out);
  tom tom_1 (
    .clk(not_13_out), .one(pc_1_oone), .two(pc_1_otwo), .three(pc_1_othree), .four(pc_1_ofour),
    .oone(tom_1_oone), .otwo(tom_1_otwo), .othree(tom_1_othree), .pfour(tom_1_pfour));
  Multiplexer #(.enable("false")) multiplexer_12 (
    .in0(inc_1_ofour), .in1(ram4bitssecure_1_out_5[3]), .out(multiplexer_12_out), .sel(and_14_out));
  Multiplexer #(.enable("false")) multiplexer_13 (
    .in0(inc_1_othree), .in1(ram4bitssecure_1_out_5[2]), .out(multiplexer_13_out), .sel(and_14_out));
  Multiplexer #(.enable("false")) multiplexer_14 (
    .in0(pc_1_otwo), .in1(mbr_3_ofive[1]), .out(multiplexer_14_out), .sel(or_21_out));
  not not_10 (not_10_out, cu_1_fifteen);
  assign out_26 = FIVE4ADD_out ? controlled_buffer_16_out : 8'bz;  // Controlled_Buffer controlled_buffer_18
  assign out_30 = SIX4ADD_out ? controlled_buffer_16_out : 8'bz;  // Controlled_Buffer controlled_buffer_19
  Multiplexer #(.enable("false")) multiplexer_15 (
    .in0(inc_1_otwo), .in1(ram4bitssecure_1_out_5[1]), .out(multiplexer_15_out), .sel(and_14_out));
  Multiplexer #(.enable("false")) multiplexer_16 (
    .in0(inc_1_oone), .in1(ram4bitssecure_1_out_5[0]), .out(multiplexer_16_out), .sel(and_14_out));
  Multiplexer #(.enable("false")) multiplexer_17 (
    .in0(pc_1_othree), .in1(mbr_3_ofive[2]), .out(multiplexer_17_out), .sel(or_21_out));
  Multiplexer #(.enable("false")) multiplexer_18 (
    .in0(pc_1_ofour), .in1(mbr_3_ofive[3]), .out(multiplexer_18_out), .sel(or_21_out));
  not not_11 (not_11_out, 1'b0);
  not not_12 (not_12_out, 1'b0);
  not not_13 (not_13_out, cu_1_fifteen);
  ram4bitssecure ram4bitssecure_1 (
    .addr(s_r_ff_1_q), .in_2(mbr_3_ofive), .readwrite(cu_1_five), .clk(not_10_out),
    .out_5(ram4bitssecure_1_out_5));
  not not_14 (not_14_out, 1'b1);
  not not_15 (not_15_out, 1'b1);
  or or_16 (or_16_out, not_15_out, tom_2_othree);
  or or_17 (or_17_out, not_14_out, tom_2_pfour);
  S_R_Flip_Flop s_r_ff_1 (.Q(s_r_ff_1_q), .reset(not_16_out), .preset(cu_1_five));  // open: S, R, clk, Qn
  not not_16 (not_16_out, cu_1_five);
  one_byte_evo one_byte_evo_1 (
    .condition(FIVE4ADD_out), .in_2(out_26), .readwrite(FIVE4ADD_out), .clk(not_11_out), .out_5(out_27));
  one_byte_evo one_byte_evo_2 (
    .condition(SIX4ADD_out), .in_2(out_30), .readwrite(SIX4ADD_out), .clk(not_12_out),
    .out_5(one_byte_evo_2_out_5));
  and and_13 (and_13_out, seven4add_out, or_31_out);
  not not_17 (not_17_out, 1'b1);
  or or_18 (or_18_out, not_17_out, tom_2_otwo);
  or or_19 (or_19_out, tom_2_oone, not_18_out);
  or or_20 (or_20_out, cu_1_six, cu_1_eight, cu_1_seven, cu_1_five, cu_1_four, cu_1_zero);
  inc inc_1 (
    .one(tom_1_oone), .two(tom_1_otwo), .three(tom_1_othree), .four(tom_1_pfour), .clk(not_13_out),
    .oone(inc_1_oone), .otwo(inc_1_otwo), .othree(inc_1_othree), .ofour(inc_1_ofour));  // open: over, zero
  tom tom_2 (
    .clk(cu_1_fifteen), .one(multiplexer_16_out), .two(multiplexer_15_out), .three(multiplexer_13_out),
    .four(multiplexer_12_out), .oone(tom_2_oone), .otwo(tom_2_otwo), .othree(tom_2_othree),
    .pfour(tom_2_pfour));
  not not_18 (not_18_out, 1'b1);
  pc pc_1 (
    .clk(cu_1_fifteen), .one(or_19_out), .two(or_18_out), .three(or_16_out), .four(or_17_out),
    .oone(pc_1_oone), .otwo(pc_1_otwo), .othree(pc_1_othree), .ofour(pc_1_ofour));
  not not_19 (not_19_out, cu_1_fifteen);
  or or_21 (or_21_out, four0_out, four1_out);
  not not_20 (out_31[2], 1'b0);
  RAM3BIT ram3bit_1 (
    .address(s_r_ff_2_q), .in_2(mbr_3_oone), .READWRITE(cu_1_five), .CLK(not_19_out), .out_5(ram3bit_1_out_5));
  S_R_Flip_Flop s_r_ff_2 (.Q(s_r_ff_2_q), .reset(not_21_out), .preset(cu_1_five));  // open: S, R, clk, Qn
  not not_21 (not_21_out, cu_1_five);
  and four0 (four0_out, cu_1_four, cu_1_ozero);
  and six0 (six0_out, cu_1_six, cu_1_ozero);
  and seven0 (seven0_out, cu_1_ozero, cu_1_seven);
  and eight0 (eight0_out, cu_1_ozero, cu_1_eight);
  and nine0 (nine0_out, cu_1_ozero, cu_1_nine);
  and five0 (five0_out, cu_1_ozero, cu_1_five);
  and five1 (five1_out, cu_1_five, cu_1_oone);
  and four1 (four1_out, cu_1_four, cu_1_oone);
  and SIX4ADD (SIX4ADD_out, or_27_out, cu_1_six);
  and FIVE4ADD (FIVE4ADD_out, cu_1_five, or_27_out);
  and seven4add (seven4add_out, cu_1_seven, or_27_out);
  ALUNEW alunew_1 (
    .OPCODE({out_31[2], 2'b00}), .RIGHT(out_27), .SUB(or_25_out), .LEFT(one_byte_evo_2_out_5),
    .RESULT(alunew_1_result), .NEGATIVE(status_register[0]), .ZERO(status_register[1]),
    .OVERFLOW(status_register[2]));
  not not_22 (not_22_out, status_register[1]);
  and and_14 (and_14_out, onebitsecure_1_out_5, or_23_out);
  or or_22 (or_22_out, and_16_out, and_15_out);
  and and_15 (and_15_out, status_register[1], cu_1_osix, and_19_out);
  or or_23 (or_23_out, cu_1_oseven, cu_1_osix);
  assign or_24_out = ram3bit_1_out_5 | mbr_3_oone;  // OR_Gate or_24, 3 bits wide
  and and_16 (and_16_out, cu_1_oseven, and_19_out, not_22_out);
  not not_23 (not_23_out, 1'b0);
  onebitsecure onebitsecure_1 (
    .addr(s_r_ff_3_q), .in_2(or_22_out), .writeread(and_19_out), .clk(not_29_out),
    .out_5(onebitsecure_1_out_5));
  S_R_Flip_Flop s_r_ff_3 (.Q(s_r_ff_3_q), .reset(not_24_out), .preset(and_19_out));  // open: S, R, clk, Qn
  not not_24 (not_24_out, and_19_out);
  and and_17 (and_17_out, or_27_out, and_19_out);
  tom tom_3 (
    .clk(not_25_out), .one(pc_2_oone), .two(pc_2_otwo), .three(pc_2_othree), .four(pc_2_ofour),
    .oone(tom_3_oone), .otwo(tom_3_otwo), .othree(tom_3_othree), .pfour(tom_3_pfour));
  one_byte_evo one_byte_evo_3 (
    .condition(and_17_out), .in_2(alunew_1_result), .readwrite(and_17_out), .clk(not_23_out),
    .out_5(one_byte_evo_3_out_5));
  not not_25 (not_25_out, in_7);
  cu cu_1 (
    .inone(pc_2_oone), .intwo(pc_2_otwo), .inthree(pc_2_othree), .infour(pc_2_ofour), .opone(or_24_out[0]),
    .optwo(or_24_out[1]), .opthree(or_24_out[2]), .fifteen(cu_1_fifteen), .nine(cu_1_nine),
    .eight(cu_1_eight), .seven(cu_1_seven), .three(cu_1_three), .five(cu_1_five), .six(cu_1_six),
    .four(cu_1_four), .one(cu_1_one), .two(cu_1_two), .zero(cu_1_zero), .oseven(cu_1_oseven),
    .othree(cu_1_othree), .ofive(cu_1_ofive), .osix(cu_1_osix), .ofour(cu_1_ofour), .oone(cu_1_oone),
    .otwo(cu_1_otwo), .ozero(cu_1_ozero));  // open: eleven, thirteen, fourteen, twelve, ten
  or or_25 (or_25_out, cu_1_ofive, cu_1_osix);
  not not_26 (not_26_out, 1'b1);
  not not_27 (not_27_out, 1'b1);
  or or_26 (or_26_out, not_26_out, tom_4_pfour);
  or or_27 (or_27_out, or_25_out, cu_1_oseven, cu_1_ofour);
  and and_18 (and_18_out, cu_1_otwo, cu_1_five);
  not not_28 (not_28_out, 1'b1);
  or or_28 (or_28_out, not_28_out, tom_4_otwo);
  or or_29 (or_29_out, not_27_out, tom_4_othree);
  not not_29 (not_29_out, cu_1_six);
  inc inc_2 (
    .one(tom_3_oone), .two(tom_3_otwo), .three(tom_3_othree), .four(tom_3_pfour), .clk(not_25_out),
    .oone(inc_2_oone), .otwo(inc_2_otwo), .othree(inc_2_othree), .ofour(inc_2_ofour));  // open: over, zero
  tom tom_4 (
    .clk(in_7), .one(inc_2_oone), .two(inc_2_otwo), .three(inc_2_othree), .four(inc_2_ofour),
    .oone(tom_4_oone), .otwo(tom_4_otwo), .othree(tom_4_othree), .pfour(tom_4_pfour));
  not not_30 (not_30_out, 1'b1);
  or or_30 (or_30_out, tom_4_oone, not_30_out);
  pc pc_2 (
    .clk(in_7), .one(or_30_out), .two(or_28_out), .three(or_29_out), .four(or_26_out), .oone(pc_2_oone),
    .otwo(pc_2_otwo), .othree(pc_2_othree), .ofour(pc_2_ofour));
  or or_31 (or_31_out, cu_1_ofive, cu_1_ofour);
  not not_31 (not_31_out, tom_4_oone);
  and and_19 (and_19_out, inc_2_oone, inc_2_otwo, inc_2_othree, not_31_out, not_32_out, not_33_out, not_34_out, not_35_out);
  not not_32 (not_32_out, inc_2_ofour);
  not not_33 (not_33_out, tom_4_otwo);
  not not_34 (not_34_out, tom_4_othree);
  not not_35 (not_35_out, tom_4_pfour);
  assign controlled_buffer_20_out = in_23 ? in_20 : 8'bz;  // Controlled_Buffer controlled_buffer_20
  assign controlled_buffer_20_out = in_21 ? in_22 : 8'bz;  // Controlled_Buffer controlled_buffer_21

  assign out_31[1:0] = 2'b00;

  // Notes on the sheet:
  //   op7 0
  //   8
  //   depends on data
  //   1
  //   op5 0
  //   2
  //   3
  //   2
  //   0
  //   op7 0
  //   4 bit
  //   op5 0
  //   op6 0
  //   op4 0
  //   only plus and minus can store in register using alu
  //   4
  //   5
  //   load
  //   minus
  //   eq
  //   add
  //   store
  //   neq
  //   print
endmodule

module ramtest (
  input  in_1,
  input  in_2,
  input  in_3,
  input  in_4,
  input  in_5,
  input  in_6,
  input  in_7,
  input  in_8,
  input  in_9,
  input  in_10,
  input  in_11,
  input  in_12,
  input  in_13
);

  main main_1 (
    .in8(in_1), .in7(in_2), .in6(in_3), .in5(in_4), .in4(in_5), .in3(in_6), .in2(in_8), .in1(in_7),
    .clk(in_9), .readwrite(in_10), .addr1(in_11), .addr2(in_12), .addr3(in_13), .addr4(in_13));  // open: out8, out7, out6, out5, out4, out3, out2, out1
endmodule

module one_bit (
  input  in_1,
  input  in_2,
  input  in_3,
  output out_4,
  output out_5
);

  wire and_1_out, and_2_out, and_3_out, not_1_out, not_2_out, or_1_out, or_2_out;

  or or_1 (or_1_out, in_2, in_3);
  not not_1 (not_1_out, and_1_out);
  and and_1 (and_1_out, in_3, in_2);
  and and_2 (and_2_out, or_1_out, not_1_out);
  or or_2 (or_2_out, in_1, and_2_out);
  and and_3 (and_3_out, in_1, and_2_out);
  not not_2 (not_2_out, and_3_out);
  and and_4 (out_4, or_2_out, not_2_out);
  or or_3 (out_5, and_3_out, and_1_out);
endmodule

module inc (
  input  one,
  input  two,
  input  three,
  input  four,
  input  clk,
  output oone,
  output otwo,
  output othree,
  output ofour,
  output over,
  output zero
);

  wire add_1bit_1_p1, add_1bit_1_p2, add_1bit_1_p4, add_1bit_2_p2, add_1bit_2_p4, add_1bit_3_p2,
       add_1bit_3_p4, add_1bit_4_p2, add_1bit_4_p4, not_1_out, not_2_out, not_3_out, not_4_out, not_5_out,
       not_6_out, not_8_out;

  xor xor_1 (over, add_1bit_1_p1, add_1bit_1_p4);
  and and_1 (oone, add_1bit_4_p2, clk);
  and and_2 (otwo, add_1bit_3_p2, clk);
  and and_3 (othree, add_1bit_2_p2, clk);
  and and_4 (ofour, add_1bit_1_p2, clk);
  // XOR_Gate xor_2 has open pins: in0=not_2_out, in1=add_1bit_4_p4, out=open
  // Add_1Bit add_1bit_1: pin names not known; wires that end beside it: add_1bit_1_p1, add_1bit_1_p2, four, add_1bit_1_p4
  // XOR_Gate xor_3 has open pins: in0=not_1_out, in1=add_1bit_4_p4, out=open
  // Add_1Bit add_1bit_2: pin names not known; wires that end beside it: add_1bit_1_p4, add_1bit_2_p2, three, add_1bit_2_p4
  not not_1 (not_1_out, 1'b1);
  not not_2 (not_2_out, 1'b1);
  // XOR_Gate xor_4 has open pins: in0=not_4_out, in1=add_1bit_4_p4, out=open
  // Add_1Bit add_1bit_3: pin names not known; wires that end beside it: add_1bit_2_p4, add_1bit_3_p2, two, add_1bit_3_p4
  not not_3 (not_3_out, add_1bit_2_p2);
  not not_4 (not_4_out, 1'b1);
  // XOR_Gate xor_5 has open pins: in0=1'b1, in1=add_1bit_4_p4, out=open
  // Add_1Bit add_1bit_4: pin names not known; wires that end beside it: add_1bit_3_p4, add_1bit_4_p2, one, add_1bit_4_p4
  not not_5 (not_5_out, add_1bit_1_p2);
  not not_6 (not_6_out, add_1bit_4_p2);
  not not_7 (add_1bit_4_p4, 1'b1);
  not not_8 (not_8_out, add_1bit_3_p2);
  and and_5 (zero, not_6_out, not_8_out, not_3_out, not_5_out);
endmodule

module pc (
  input  clk,
  input  one,
  input  two,
  input  three,
  input  four,
  output oone,
  output otwo,
  output othree,
  output ofour
);

  wire and_1_out, and_2_out, and_3_out, and_4_out, not_1_out, not_2_out, not_3_out, not_4_out, undriven,
       undriven_2, undriven_3, undriven_4;

  and and_1 (and_1_out, clk, one);
  and and_2 (and_2_out, clk, two);
  and and_3 (and_3_out, clk, three);
  and and_4 (and_4_out, clk, four);
  not not_1 (not_1_out, and_1_out);
  not not_2 (not_2_out, and_2_out);
  not not_3 (not_3_out, and_3_out);
  not not_4 (not_4_out, and_4_out);
  S_R_Flip_Flop s_r_ff_1 (.S(undriven), .Q(oone), .reset(not_1_out), .preset(and_1_out));  // open: R, clk, Qn
  S_R_Flip_Flop s_r_ff_2 (.S(undriven_2), .Q(otwo), .reset(not_2_out), .preset(and_2_out));  // open: R, clk, Qn
  S_R_Flip_Flop s_r_ff_3 (.S(undriven_3), .Q(othree), .reset(not_3_out), .preset(and_3_out));  // open: R, clk, Qn
  S_R_Flip_Flop s_r_ff_4 (.S(undriven_4), .Q(ofour), .reset(not_4_out), .preset(and_4_out));  // open: R, clk, Qn
endmodule

module tom (
  input  clk,
  input  one,
  input  two,
  input  three,
  input  four,
  output oone,
  output otwo,
  output othree,
  output pfour
);

  wire and_1_out, and_2_out, and_3_out, and_4_out, not_1_out, not_2_out, not_3_out, not_4_out, not_5_out,
       not_6_out, not_7_out, not_8_out, s_r_ff_1_q, s_r_ff_2_q, s_r_ff_3_q, s_r_ff_4_q, undriven, undriven_2,
       undriven_3, undriven_4;

  not not_1 (not_1_out, one);
  and and_1 (and_1_out, not_1_out, not_2_out);
  not not_2 (not_2_out, clk);
  not not_3 (not_3_out, two);
  and and_2 (and_2_out, not_3_out, not_4_out);
  not not_4 (not_4_out, clk);
  not not_5 (not_5_out, three);
  and and_3 (and_3_out, not_5_out, not_6_out);
  not not_6 (not_6_out, clk);
  not not_7 (not_7_out, four);
  not not_8 (not_8_out, clk);
  S_R_Flip_Flop s_r_ff_1 (.S(undriven), .Q(s_r_ff_1_q), .reset(and_1_out), .preset(one));  // open: R, clk, Qn
  S_R_Flip_Flop s_r_ff_2 (.S(undriven_2), .Q(s_r_ff_2_q), .reset(and_2_out), .preset(two));  // open: R, clk, Qn
  S_R_Flip_Flop s_r_ff_3 (.S(undriven_3), .Q(s_r_ff_3_q), .reset(and_3_out), .preset(three));  // open: R, clk, Qn
  S_R_Flip_Flop s_r_ff_4 (.S(undriven_4), .Q(s_r_ff_4_q), .reset(and_4_out), .preset(four));  // open: R, clk, Qn
  and and_4 (and_4_out, not_7_out, not_8_out);
  and and_5 (oone, clk, s_r_ff_1_q);
  and and_6 (otwo, clk, s_r_ff_2_q);
  and and_7 (othree, clk, s_r_ff_3_q);
  and and_8 (pfour, clk, s_r_ff_4_q);
endmodule

module mar (
  input  clk,
  input  one,
  input  two,
  input  three,
  input  four,
  output oone,
  output otwo,
  output othree,
  output ofour
);

  wire and_1_out, and_2_out, and_3_out, and_4_out, not_1_out, not_2_out, not_3_out, not_4_out, undriven,
       undriven_2, undriven_3, undriven_4;

  and and_1 (and_1_out, clk, one);
  and and_2 (and_2_out, clk, two);
  and and_3 (and_3_out, clk, three);
  and and_4 (and_4_out, clk, four);
  not not_1 (not_1_out, and_1_out);
  not not_2 (not_2_out, and_2_out);
  not not_3 (not_3_out, and_3_out);
  not not_4 (not_4_out, and_4_out);
  S_R_Flip_Flop s_r_ff_1 (.S(undriven), .Q(oone), .reset(not_1_out), .preset(and_1_out));  // open: R, clk, Qn
  S_R_Flip_Flop s_r_ff_2 (.S(undriven_2), .Q(otwo), .reset(not_2_out), .preset(and_2_out));  // open: R, clk, Qn
  S_R_Flip_Flop s_r_ff_3 (.S(undriven_3), .Q(othree), .reset(not_3_out), .preset(and_3_out));  // open: R, clk, Qn
  S_R_Flip_Flop s_r_ff_4 (.S(undriven_4), .Q(ofour), .reset(not_4_out), .preset(and_4_out));  // open: R, clk, Qn
endmodule

module mbr (
  input  clk,
  input  one,
  input  two,
  input  three,
  input  four,
  input  five,
  input  six,
  input  seven,
  input  eight,
  output oone,
  output otwo,
  output othree,
  output ofour,
  output ofive,
  output osix,
  output oseven,
  output oeight
);

  wire and_1_out, and_2_out, and_3_out, and_4_out, and_5_out, and_6_out, and_7_out, and_8_out, not_1_out,
       not_2_out, not_3_out, not_4_out, not_5_out, not_6_out, not_7_out, not_8_out, not_9_out, not_10_out,
       not_11_out, not_12_out, not_13_out, not_14_out, not_15_out, not_16_out, s_r_ff_1_q, s_r_ff_2_q,
       s_r_ff_3_q, s_r_ff_4_q, s_r_ff_5_q, s_r_ff_6_q, s_r_ff_7_q, s_r_ff_8_q, undriven, undriven_2,
       undriven_3, undriven_4, undriven_5, undriven_6, undriven_7, undriven_8;

  not not_1 (not_1_out, one);
  and and_1 (and_1_out, not_1_out, not_2_out);
  not not_2 (not_2_out, clk);
  not not_3 (not_3_out, two);
  and and_2 (and_2_out, not_3_out, not_4_out);
  not not_4 (not_4_out, clk);
  not not_5 (not_5_out, three);
  and and_3 (and_3_out, not_5_out, not_6_out);
  not not_6 (not_6_out, clk);
  not not_7 (not_7_out, four);
  not not_8 (not_8_out, clk);
  not not_9 (not_9_out, five);
  and and_4 (and_4_out, not_9_out, not_10_out);
  not not_10 (not_10_out, clk);
  not not_11 (not_11_out, six);
  and and_5 (and_5_out, not_11_out, not_12_out);
  not not_12 (not_12_out, clk);
  not not_13 (not_13_out, seven);
  and and_6 (and_6_out, not_13_out, not_14_out);
  not not_14 (not_14_out, clk);
  not not_15 (not_15_out, eight);
  not not_16 (not_16_out, clk);
  S_R_Flip_Flop s_r_ff_1 (.S(undriven), .Q(s_r_ff_1_q), .reset(and_1_out), .preset(one));  // open: R, clk, Qn
  S_R_Flip_Flop s_r_ff_2 (.S(undriven_2), .Q(s_r_ff_2_q), .reset(and_2_out), .preset(two));  // open: R, clk, Qn
  S_R_Flip_Flop s_r_ff_3 (.S(undriven_3), .Q(s_r_ff_3_q), .reset(and_3_out), .preset(three));  // open: R, clk, Qn
  S_R_Flip_Flop s_r_ff_4 (.S(undriven_4), .Q(s_r_ff_4_q), .reset(and_7_out), .preset(four));  // open: R, clk, Qn
  and and_7 (and_7_out, not_7_out, not_8_out);
  S_R_Flip_Flop s_r_ff_5 (.S(undriven_5), .Q(s_r_ff_5_q), .reset(and_4_out), .preset(five));  // open: R, clk, Qn
  S_R_Flip_Flop s_r_ff_6 (.S(undriven_6), .Q(s_r_ff_6_q), .reset(and_5_out), .preset(six));  // open: R, clk, Qn
  S_R_Flip_Flop s_r_ff_7 (.S(undriven_7), .Q(s_r_ff_7_q), .reset(and_6_out), .preset(seven));  // open: R, clk, Qn
  S_R_Flip_Flop s_r_ff_8 (.S(undriven_8), .Q(s_r_ff_8_q), .reset(and_8_out), .preset(eight));  // open: R, clk, Qn
  and and_8 (and_8_out, not_15_out, not_16_out);
  and and_9 (oone, clk, s_r_ff_1_q);
  and and_10 (otwo, clk, s_r_ff_2_q);
  and and_11 (othree, clk, s_r_ff_3_q);
  and and_12 (ofour, clk, s_r_ff_4_q);
  and and_13 (ofive, clk, s_r_ff_5_q);
  and and_14 (osix, clk, s_r_ff_6_q);
  and and_15 (oseven, clk, s_r_ff_7_q);
  and and_16 (oeight, clk, s_r_ff_8_q);
endmodule

module cu (
  input  inone,
  input  intwo,
  input  inthree,
  input  infour,
  input  opone,
  input  optwo,
  input  opthree,
  output fifteen,
  output eleven,
  output thirteen,
  output fourteen,
  output twelve,
  output nine,
  output ten,
  output eight,
  output seven,
  output three,
  output five,
  output six,
  output four,
  output one,
  output two,
  output zero,
  output oseven,
  output othree,
  output ofive,
  output osix,
  output ofour,
  output oone,
  output otwo,
  output ozero
);

  wire not_1_out, not_2_out, not_3_out, not_4_out, not_5_out, not_6_out, not_7_out, not_8_out, not_9_out,
       not_10_out, not_11_out, not_12_out, not_13_out, not_14_out, not_15_out, not_16_out, not_17_out,
       not_18_out, not_19_out, not_20_out, not_21_out, not_22_out, not_23_out, not_24_out, not_25_out,
       not_26_out, not_27_out, not_28_out, not_29_out, not_30_out, not_31_out, not_32_out, not_33_out,
       not_34_out, not_35_out, not_36_out, not_37_out, not_38_out, not_39_out, not_40_out, not_41_out,
       not_42_out, not_43_out, not_44_out;

  not not_1 (not_1_out, opthree);
  not not_2 (not_2_out, inthree);
  not not_3 (not_3_out, intwo);
  not not_4 (not_4_out, inone);
  not not_5 (not_5_out, inthree);
  and and_1 (oseven, opone, optwo, opthree);
  and and_2 (othree, opone, optwo, not_1_out);
  not not_6 (not_6_out, optwo);
  and and_3 (ofive, opone, opone, not_6_out, opthree);
  not not_7 (not_7_out, opone);
  and and_4 (osix, not_7_out, optwo, opthree);
  not not_8 (not_8_out, opone);
  not not_9 (not_9_out, optwo);
  not not_10 (not_10_out, optwo);
  not not_11 (not_11_out, opthree);
  not not_12 (not_12_out, opone);
  not not_13 (not_13_out, opthree);
  not not_14 (not_14_out, opone);
  not not_15 (not_15_out, optwo);
  not not_16 (not_16_out, opthree);
  and and_5 (fifteen, inone, intwo, inthree, infour);
  and and_6 (eleven, inone, intwo, not_2_out, infour);
  and and_7 (thirteen, inone, not_3_out, inthree, infour);
  and and_8 (fourteen, not_4_out, intwo, inthree, infour);
  not not_17 (not_17_out, inone);
  and and_9 (twelve, not_17_out, not_18_out, inthree, infour);
  not not_18 (not_18_out, intwo);
  not not_19 (not_19_out, intwo);
  and and_10 (nine, inone, not_19_out, not_20_out, infour);
  not not_20 (not_20_out, inthree);
  not not_21 (not_21_out, inone);
  and and_11 (ten, infour, not_21_out, intwo, not_22_out);
  not not_22 (not_22_out, inthree);
  not not_23 (not_23_out, inone);
  and and_12 (eight, infour, not_23_out, not_24_out, not_25_out);
  not not_24 (not_24_out, intwo);
  not not_25 (not_25_out, inthree);
  not not_26 (not_26_out, infour);
  and and_13 (seven, not_26_out, inone, intwo, inthree);
  not not_27 (not_27_out, infour);
  and and_14 (three, not_27_out, inone, intwo, not_5_out);
  and and_15 (five, inone, inone, not_28_out, inthree, not_29_out);
  not not_28 (not_28_out, intwo);
  not not_29 (not_29_out, infour);
  not not_30 (not_30_out, inone);
  and and_16 (six, not_30_out, intwo, inthree, not_31_out);
  not not_31 (not_31_out, infour);
  not not_32 (not_32_out, inone);
  and and_17 (four, not_32_out, not_33_out, inthree, not_34_out);
  not not_33 (not_33_out, intwo);
  not not_34 (not_34_out, infour);
  not not_35 (not_35_out, infour);
  not not_36 (not_36_out, intwo);
  and and_18 (one, not_35_out, inone, not_36_out, not_37_out);
  not not_37 (not_37_out, inthree);
  not not_38 (not_38_out, infour);
  not not_39 (not_39_out, inone);
  and and_19 (two, not_38_out, not_39_out, intwo, not_40_out);
  not not_40 (not_40_out, inthree);
  not not_41 (not_41_out, infour);
  not not_42 (not_42_out, inone);
  not not_43 (not_43_out, intwo);
  and and_20 (zero, not_41_out, not_42_out, not_43_out, not_44_out);
  not not_44 (not_44_out, inthree);
  and and_21 (ofour, not_8_out, not_9_out, opthree);
  and and_22 (oone, opone, not_10_out, not_11_out);
  and and_23 (otwo, not_12_out, optwo, not_13_out);
  and and_24 (ozero, not_14_out, not_15_out, not_16_out);
endmodule

module gate (
  input  c1,
  input  d1,
  input  c2,
  input  d2,
  input  c3,
  input  d3,
  input  c4,
  input  d4,
  output oone,
  output otwo,
  output othree,
  output ofour
);

  wire and_1_out, and_2_out, and_3_out, and_4_out, and_5_out, and_6_out, and_7_out, and_8_out, and_9_out,
       and_10_out, and_11_out, and_12_out, and_13_out, and_14_out, and_15_out, and_16_out;

  or or_1 (oone, and_1_out, and_2_out, and_3_out, and_4_out);
  or or_2 (otwo, and_5_out, and_6_out, and_7_out, and_8_out);
  or or_3 (othree, and_9_out, and_10_out, and_11_out, and_12_out);
  or or_4 (ofour, and_13_out, and_14_out, and_15_out, and_16_out);
  and and_1 (and_1_out, c1, d1);
  and and_2 (and_2_out, c2, d1);
  and and_3 (and_3_out, c3, d1);
  and and_4 (and_4_out, c4, d1);
  and and_5 (and_5_out, c1, d2);
  and and_6 (and_6_out, c2, d2);
  and and_7 (and_7_out, c3, d2);
  and and_8 (and_8_out, c4, d2);
  and and_9 (and_9_out, c1, d3);
  and and_10 (and_10_out, c2, d3);
  and and_11 (and_11_out, c3, d3);
  and and_12 (and_12_out, c4, d3);
  and and_13 (and_13_out, c1, d4);
  and and_14 (and_14_out, c2, d4);
  and and_15 (and_15_out, c3, d4);
  and and_16 (and_16_out, c4, d4);
endmodule

module gate8bits (
  input  c1,
  input  d1,
  input  c2,
  input  d2,
  input  c3,
  input  d3,
  input  c4,
  input  d4,
  input  d5,
  input  d6,
  input  d7,
  input  d8,
  output o1,
  output o2,
  output o3,
  output o4,
  output o5,
  output o6,
  output o7,
  output o8
);

  wire and_1_out, and_2_out, and_3_out, and_4_out, and_5_out, and_6_out, and_7_out, and_8_out, and_9_out,
       and_10_out, and_11_out, and_12_out, and_13_out, and_14_out, and_15_out, and_16_out, and_17_out,
       and_18_out, and_19_out, and_20_out, and_21_out, and_22_out, and_23_out, and_24_out, and_25_out,
       and_26_out, and_27_out, and_28_out, and_29_out, and_30_out, and_31_out, and_32_out, not_1_out,
       not_2_out, not_3_out, not_4_out, not_5_out, not_6_out, not_7_out, not_8_out, or_1_out, or_2_out,
       or_3_out, or_4_out, or_5_out, or_6_out, or_7_out, or_8_out;

  or or_1 (or_1_out, and_17_out, and_18_out, and_19_out, and_20_out);
  or or_2 (or_2_out, and_21_out, and_22_out, and_23_out, and_24_out);
  or or_3 (or_3_out, and_25_out, and_26_out, and_27_out, and_28_out);
  or or_4 (or_4_out, and_29_out, and_30_out, and_31_out, and_32_out);
  or or_5 (or_5_out, and_1_out, and_2_out, and_3_out, and_4_out);
  or or_6 (or_6_out, and_5_out, and_6_out, and_7_out, and_8_out);
  or or_7 (or_7_out, and_9_out, and_10_out, and_11_out, and_12_out);
  or or_8 (or_8_out, and_13_out, and_14_out, and_15_out, and_16_out);
  and and_1 (and_1_out, c1, d5);
  and and_2 (and_2_out, c2, d5);
  and and_3 (and_3_out, c3, d5);
  and and_4 (and_4_out, c4, d5);
  and and_5 (and_5_out, c1, d6);
  and and_6 (and_6_out, c2, d6);
  and and_7 (and_7_out, c3, d6);
  and and_8 (and_8_out, c4, d6);
  and and_9 (and_9_out, c1, d7);
  and and_10 (and_10_out, c2, d7);
  and and_11 (and_11_out, c3, d7);
  and and_12 (and_12_out, c4, d7);
  and and_13 (and_13_out, c1, d8);
  and and_14 (and_14_out, c2, d8);
  and and_15 (and_15_out, c3, d8);
  and and_16 (and_16_out, c4, d8);
  and and_17 (and_17_out, c1, d1);
  and and_18 (and_18_out, c2, d1);
  and and_19 (and_19_out, c3, d1);
  and and_20 (and_20_out, c4, d1);
  and and_21 (and_21_out, c1, d2);
  and and_22 (and_22_out, c2, d2);
  and and_23 (and_23_out, c3, d2);
  and and_24 (and_24_out, c4, d2);
  and and_25 (and_25_out, c1, d3);
  and and_26 (and_26_out, c2, d3);
  and and_27 (and_27_out, c3, d3);
  and and_28 (and_28_out, c4, d3);
  and and_29 (and_29_out, c1, d4);
  and and_30 (and_30_out, c2, d4);
  and and_31 (and_31_out, c3, d4);
  and and_32 (and_32_out, c4, d4);
  S_R_Flip_Flop s_r_ff_1 (.Q(o1), .reset(not_1_out), .preset(or_1_out));  // open: S, R, clk, Qn
  not not_1 (not_1_out, or_1_out);
  S_R_Flip_Flop s_r_ff_2 (.Q(o3), .reset(not_2_out), .preset(or_3_out));  // open: S, R, clk, Qn
  not not_2 (not_2_out, or_3_out);
  S_R_Flip_Flop s_r_ff_3 (.Q(o4), .reset(not_3_out), .preset(or_4_out));  // open: S, R, clk, Qn
  not not_3 (not_3_out, or_4_out);
  S_R_Flip_Flop s_r_ff_4 (.Q(o5), .reset(not_4_out), .preset(or_5_out));  // open: S, R, clk, Qn
  not not_4 (not_4_out, or_5_out);
  S_R_Flip_Flop s_r_ff_5 (.Q(o6), .reset(not_5_out), .preset(or_6_out));  // open: S, R, clk, Qn
  not not_5 (not_5_out, or_6_out);
  S_R_Flip_Flop s_r_ff_6 (.Q(o7), .reset(not_6_out), .preset(or_7_out));  // open: S, R, clk, Qn
  not not_6 (not_6_out, or_7_out);
  S_R_Flip_Flop s_r_ff_7 (.Q(o8), .reset(not_7_out), .preset(or_8_out));  // open: S, R, clk, Qn
  not not_7 (not_7_out, or_8_out);
  S_R_Flip_Flop s_r_ff_8 (.Q(o2), .reset(not_8_out), .preset(or_2_out));  // open: S, R, clk, Qn
  not not_8 (not_8_out, or_2_out);
endmodule

module muuuuux (
  input  A1,
  input  B1,
  input  A2,
  input  B2,
  input  A3,
  input  B3,
  input  A4,
  input  B4,
  input  A5,
  input  B5,
  input  A6,
  input  B6,
  input  A7,
  input  B7,
  input  A8,
  input  B8,
  input  condition,
  output out1,
  output out2,
  output out3,
  output out4,
  output out5,
  output out6,
  output out7,
  output out8
);

  Multiplexer #(.enable("false")) multiplexer_1 (.in0(A1), .in1(B1), .out(out1), .sel(condition));
  Multiplexer #(.enable("false")) multiplexer_2 (.in0(A2), .in1(B2), .out(out2), .sel(condition));
  Multiplexer #(.enable("false")) multiplexer_3 (.in0(A3), .in1(B3), .out(out3), .sel(condition));
  Multiplexer #(.enable("false")) multiplexer_4 (.in0(A4), .in1(B4), .out(out4), .sel(condition));
  Multiplexer #(.enable("false")) multiplexer_5 (.in0(A5), .in1(B5), .out(out5), .sel(condition));
  Multiplexer #(.enable("false")) multiplexer_6 (.in0(A6), .in1(B6), .out(out6), .sel(condition));
  Multiplexer #(.enable("false")) multiplexer_7 (.in0(A7), .in1(B7), .out(out7), .sel(condition));
  Multiplexer #(.enable("false")) multiplexer_8 (.in0(A8), .in1(B8), .out(out8), .sel(condition));
endmodule

module MBRtoIR (
  input  one,
  input  in_2,
  input  in_3,
  input  in_4,
  input  in_5,
  input  in_6,
  input  in_7,
  input  in_8,
  input  in_9,
  output out_10,
  output out_11,
  output out_12,
  output out_13,
  output out_14,
  output out_15,
  output out_16,
  output out_17
);

  wire and_1_out, and_2_out, and_3_out, and_4_out, and_5_out, and_6_out, and_7_out, and_8_out, not_1_out,
       not_2_out, not_3_out, not_4_out, not_5_out, not_6_out, not_7_out, not_8_out;

  and and_1 (and_1_out, one, in_9);
  and and_2 (and_2_out, in_2, in_9);
  and and_3 (and_3_out, in_3, in_9);
  and and_4 (and_4_out, in_4, in_9);
  and and_5 (and_5_out, in_5, in_9);
  and and_6 (and_6_out, in_6, in_9);
  and and_7 (and_7_out, in_7, in_9);
  and and_8 (and_8_out, in_8, in_9);
  S_R_Flip_Flop s_r_ff_1 (.Q(out_10), .reset(not_1_out), .preset(and_1_out));  // open: S, R, clk, Qn
  not not_1 (not_1_out, and_1_out);
  S_R_Flip_Flop s_r_ff_2 (.Q(out_11), .reset(not_2_out), .preset(and_2_out));  // open: S, R, clk, Qn
  not not_2 (not_2_out, and_2_out);
  S_R_Flip_Flop s_r_ff_3 (.Q(out_12), .reset(not_3_out), .preset(and_3_out));  // open: S, R, clk, Qn
  not not_3 (not_3_out, and_3_out);
  S_R_Flip_Flop s_r_ff_4 (.Q(out_13), .reset(not_4_out), .preset(and_4_out));  // open: S, R, clk, Qn
  not not_4 (not_4_out, and_4_out);
  S_R_Flip_Flop s_r_ff_5 (.Q(out_14), .reset(not_5_out), .preset(and_5_out));  // open: S, R, clk, Qn
  not not_5 (not_5_out, and_5_out);
  S_R_Flip_Flop s_r_ff_6 (.Q(out_15), .reset(not_6_out), .preset(and_6_out));  // open: S, R, clk, Qn
  not not_6 (not_6_out, and_6_out);
  S_R_Flip_Flop s_r_ff_7 (.Q(out_16), .reset(not_7_out), .preset(and_7_out));  // open: S, R, clk, Qn
  not not_7 (not_7_out, and_7_out);
  S_R_Flip_Flop s_r_ff_8 (.Q(out_17), .reset(not_8_out), .preset(and_8_out));  // open: S, R, clk, Qn
  not not_8 (not_8_out, and_8_out);
endmodule

module one_byte_evo (
  input  condition,
  input  [7:0] in_2,
  input  readwrite,
  input  clk,
  output [7:0] out_5
);

  wire and_2_out, and_3_out, and_4_out, and_5_out, and_6_out, and_7_out, and_8_out, and_9_out, and_10_out,
       and_11_out, and_12_out, and_13_out, and_14_out, and_15_out, and_16_out, and_17_out, not_1_out,
       not_2_out, not_3_out, not_4_out, not_5_out, not_6_out, not_7_out, not_8_out, not_9_out, s_r_ff_1_q,
       s_r_ff_2_q, s_r_ff_3_q, s_r_ff_4_q, s_r_ff_5_q, s_r_ff_6_q, s_r_ff_7_q, s_r_ff_8_q;
  wire [7:0] and_1_out;

  assign and_1_out = {8{condition}} & in_2;  // AND_Gate and_1, 8 bits wide
  not not_1 (not_1_out, and_1_out[6]);
  not not_2 (not_2_out, and_1_out[7]);
  not not_3 (not_3_out, and_1_out[5]);
  not not_4 (not_4_out, and_1_out[4]);
  not not_5 (not_5_out, and_1_out[0]);
  not not_6 (not_6_out, and_1_out[1]);
  not not_7 (not_7_out, and_1_out[2]);
  not not_8 (not_8_out, and_1_out[3]);
  and and_2 (and_2_out, readwrite, and_1_out[0], 1'b1);
  and and_3 (and_3_out, readwrite, and_1_out[1], 1'b1);
  and and_4 (and_4_out, readwrite, and_1_out[2], 1'b1);
  and and_5 (and_5_out, 1'b1, not_7_out, readwrite);
  and and_6 (and_6_out, 1'b1, not_8_out, readwrite);
  and and_7 (and_7_out, readwrite, and_1_out[4], 1'b1);
  and and_8 (and_8_out, readwrite, and_1_out[5], 1'b1);
  and and_9 (and_9_out, readwrite, and_1_out[6], 1'b1);
  and and_10 (and_10_out, 1'b1, not_1_out, readwrite);
  and and_11 (and_11_out, 1'b1, not_2_out, readwrite);
  and and_12 (and_12_out, 1'b1, not_5_out, readwrite);
  and and_13 (and_13_out, 1'b1, not_6_out, readwrite);
  and and_14 (and_14_out, readwrite, and_1_out[3], 1'b1);
  and and_15 (and_15_out, 1'b1, not_4_out, readwrite);
  and and_16 (and_16_out, 1'b1, not_3_out, readwrite);
  and and_17 (and_17_out, readwrite, and_1_out[7], 1'b1);
  not not_9 (not_9_out, readwrite);
  S_R_Flip_Flop s_r_ff_1 (.clk(clk), .Q(s_r_ff_1_q), .reset(and_12_out), .preset(and_2_out));  // open: S, R, Qn
  S_R_Flip_Flop s_r_ff_2 (.clk(clk), .Q(s_r_ff_2_q), .reset(and_13_out), .preset(and_3_out));  // open: S, R, Qn
  S_R_Flip_Flop s_r_ff_3 (.clk(clk), .Q(s_r_ff_3_q), .reset(and_5_out), .preset(and_4_out));  // open: S, R, Qn
  S_R_Flip_Flop s_r_ff_4 (.clk(clk), .Q(s_r_ff_4_q), .reset(and_6_out), .preset(and_14_out));  // open: S, R, Qn
  S_R_Flip_Flop s_r_ff_5 (.clk(clk), .Q(s_r_ff_5_q), .reset(and_15_out), .preset(and_7_out));  // open: S, R, Qn
  S_R_Flip_Flop s_r_ff_6 (.clk(clk), .Q(s_r_ff_6_q), .reset(and_16_out), .preset(and_8_out));  // open: S, R, Qn
  S_R_Flip_Flop s_r_ff_7 (.clk(clk), .Q(s_r_ff_7_q), .reset(and_10_out), .preset(and_9_out));  // open: S, R, Qn
  S_R_Flip_Flop s_r_ff_8 (.clk(clk), .Q(s_r_ff_8_q), .reset(and_11_out), .preset(and_17_out));  // open: S, R, Qn
  and and_18 (out_5[1], s_r_ff_2_q, not_9_out, clk, 1'b1);
  and and_19 (out_5[2], s_r_ff_3_q, not_9_out, clk, 1'b1);
  and and_20 (out_5[3], 1'b1, s_r_ff_4_q, not_9_out, clk);
  and and_21 (out_5[5], s_r_ff_6_q, not_9_out, clk, 1'b1);
  and and_22 (out_5[6], s_r_ff_7_q, not_9_out, clk, 1'b1);
  and and_23 (out_5[7], 1'b1, s_r_ff_8_q, not_9_out, clk);
  and and_24 (out_5[0], s_r_ff_1_q, not_9_out, clk, 1'b1);
  and and_25 (out_5[4], s_r_ff_5_q, not_9_out, clk, 1'b1);

  // Notes on the sheet:
  //   5
  //   addr
endmodule

module fourbitram (
  input  condition,
  input  [3:0] in_2,
  input  readorwrite,
  input  clk,
  output [3:0] out_5
);

  wire and_2_out, and_3_out, and_4_out, and_5_out, and_6_out, and_7_out, and_8_out, and_9_out, not_1_out,
       not_2_out, not_3_out, not_4_out, not_5_out, s_r_ff_1_q, s_r_ff_2_q, s_r_ff_3_q, s_r_ff_4_q;
  wire [3:0] and_1_out;

  assign and_1_out = {4{condition}} & in_2;  // AND_Gate and_1, 4 bits wide
  not not_1 (not_1_out, and_1_out[0]);
  not not_2 (not_2_out, and_1_out[1]);
  not not_3 (not_3_out, and_1_out[2]);
  not not_4 (not_4_out, and_1_out[3]);
  and and_2 (and_2_out, readorwrite, and_1_out[0], 1'b1);
  and and_3 (and_3_out, readorwrite, and_1_out[1], 1'b1);
  and and_4 (and_4_out, readorwrite, and_1_out[2], 1'b1);
  and and_5 (and_5_out, 1'b1, not_3_out, readorwrite);
  and and_6 (and_6_out, 1'b1, not_4_out, readorwrite);
  and and_7 (and_7_out, 1'b1, not_1_out, readorwrite);
  and and_8 (and_8_out, 1'b1, not_2_out, readorwrite);
  and and_9 (and_9_out, readorwrite, and_1_out[3], 1'b1);
  not not_5 (not_5_out, readorwrite);
  S_R_Flip_Flop s_r_ff_1 (.clk(clk), .Q(s_r_ff_1_q), .reset(and_7_out), .preset(and_2_out));  // open: S, R, Qn
  S_R_Flip_Flop s_r_ff_2 (.clk(clk), .Q(s_r_ff_2_q), .reset(and_8_out), .preset(and_3_out));  // open: S, R, Qn
  S_R_Flip_Flop s_r_ff_3 (.clk(clk), .Q(s_r_ff_3_q), .reset(and_5_out), .preset(and_4_out));  // open: S, R, Qn
  S_R_Flip_Flop s_r_ff_4 (.clk(clk), .Q(s_r_ff_4_q), .reset(and_6_out), .preset(and_9_out));  // open: S, R, Qn
  and and_10 (out_5[1], s_r_ff_2_q, not_5_out, clk, 1'b1);
  and and_11 (out_5[2], s_r_ff_3_q, not_5_out, clk, 1'b1);
  and and_12 (out_5[3], 1'b1, s_r_ff_4_q, not_5_out, clk);
  and and_13 (out_5[0], s_r_ff_1_q, not_5_out, clk, 1'b1);

  // Notes on the sheet:
  //   addr
endmodule

module Adder1bit (
  input  a,
  input  b,
  input  Cin,
  output Sum,
  output Cout
);

  wire and_1_out, and_2_out, xor_1_out;

  xor xor_1 (xor_1_out, a, b);
  xor xor_2 (Sum, xor_1_out, Cin);
  and and_1 (and_1_out, xor_1_out, Cin);
  and and_2 (and_2_out, b, a);
  or or_1 (Cout, and_1_out, and_2_out);
endmodule

module ALUNEW (
  input  [2:0] OPCODE,
  input  [7:0] RIGHT,
  input  SUB,
  input  [7:0] LEFT,
  output [7:0] RESULT,
  output NEGATIVE,
  output ZERO,
  output OVERFLOW
);

  wire alu1bit_1_out_8, alu1bit_2_out_8, alu1bit_3_out_8, alu1bit_4_out_8, alu1bit_5_out_8, alu1bit_6_out_8,
       alu1bit_7_out_8, alu1bit_8_out_9, and_1_out, and_2_out, and_3_out, and_4_out, and_5_out, and_6_out,
       and_7_out, and_8_out, not_1_out, or_1_out, or_2_out, or_3_out, or_4_out, or_5_out, or_6_out, or_7_out,
       or_8_out, twocomplementnew_1_out_10, twocomplementnew_1_out_11, twocomplementnew_1_out_12,
       twocomplementnew_1_out_13, twocomplementnew_1_out_14, twocomplementnew_1_out_15,
       twocomplementnew_1_out_16, twocomplementnew_1_out_17;

  not not_1 (not_1_out, SUB);
  and and_1 (and_1_out, LEFT[0], not_1_out);
  and and_2 (and_2_out, LEFT[1], not_1_out);
  and and_3 (and_3_out, LEFT[2], not_1_out);
  and and_4 (and_4_out, LEFT[3], not_1_out);
  and and_5 (and_5_out, LEFT[4], not_1_out);
  and and_6 (and_6_out, LEFT[5], not_1_out);
  and and_7 (and_7_out, LEFT[6], not_1_out);
  and and_8 (and_8_out, LEFT[7], not_1_out);
  ALU1BIT alu1bit_1 (
    .in_2(RIGHT[0]), .in_3(or_1_out), .in_1(OPCODE), .in_6(alu1bit_8_out_9), .out_7(RESULT[0]),
    .out_8(alu1bit_1_out_8));  // open: in_5, in_4, out_9
  twoComplementnew twocomplementnew_1 (
    .in_1(SUB), .in_2(LEFT[1]), .in_3(LEFT[4]), .in_4(LEFT[6]), .in_5(LEFT[3]), .in_6(LEFT[5]),
    .in_7(LEFT[2]), .in_8(LEFT[7]), .in_9(LEFT[0]), .out_10(twocomplementnew_1_out_10),
    .out_11(twocomplementnew_1_out_11), .out_12(twocomplementnew_1_out_12),
    .out_13(twocomplementnew_1_out_13), .out_14(twocomplementnew_1_out_14),
    .out_15(twocomplementnew_1_out_15), .out_16(twocomplementnew_1_out_16), .out_17(twocomplementnew_1_out_17));
  ALU1BIT alu1bit_2 (
    .in_2(RIGHT[1]), .in_3(or_2_out), .in_5(alu1bit_1_out_8), .in_1(OPCODE), .in_6(1'b0), .out_7(RESULT[1]),
    .out_8(alu1bit_2_out_8));  // open: in_4, out_9
  ALU1BIT alu1bit_3 (
    .in_2(RIGHT[2]), .in_3(or_3_out), .in_5(alu1bit_2_out_8), .in_1(OPCODE), .in_6(1'b0), .out_7(RESULT[2]),
    .out_8(alu1bit_3_out_8));  // open: in_4, out_9
  ALU1BIT alu1bit_4 (
    .in_2(RIGHT[3]), .in_3(or_4_out), .in_5(alu1bit_3_out_8), .in_1(OPCODE), .in_6(1'b0), .out_7(RESULT[3]),
    .out_8(alu1bit_4_out_8));  // open: in_4, out_9
  ALU1BIT alu1bit_5 (
    .in_2(RIGHT[4]), .in_3(or_5_out), .in_5(alu1bit_4_out_8), .in_1(OPCODE), .in_6(1'b0), .out_7(RESULT[4]),
    .out_8(alu1bit_5_out_8));  // open: in_4, out_9
  ALU1BIT alu1bit_6 (
    .in_2(RIGHT[5]), .in_3(or_6_out), .in_5(alu1bit_5_out_8), .in_1(OPCODE), .in_6(1'b0), .out_7(RESULT[5]),
    .out_8(alu1bit_6_out_8));  // open: in_4, out_9
  ALU1BIT alu1bit_7 (
    .in_2(RIGHT[6]), .in_3(or_7_out), .in_5(alu1bit_6_out_8), .in_1(OPCODE), .in_6(1'b0), .out_7(RESULT[6]),
    .out_8(alu1bit_7_out_8));  // open: in_4, out_9
  ALU1BIT alu1bit_8 (
    .in_2(RIGHT[7]), .in_3(or_8_out), .in_5(alu1bit_7_out_8), .in_1(OPCODE), .in_6(1'b0), .out_7(NEGATIVE),
    .out_8(OVERFLOW), .out_9(alu1bit_8_out_9));  // open: in_4
  or or_1 (or_1_out, twocomplementnew_1_out_12, and_1_out);
  or or_2 (or_2_out, twocomplementnew_1_out_14, and_2_out);
  or or_3 (or_3_out, twocomplementnew_1_out_16, and_3_out);
  or or_4 (or_4_out, twocomplementnew_1_out_11, and_4_out);
  or or_5 (or_5_out, twocomplementnew_1_out_13, and_5_out);
  or or_6 (or_6_out, twocomplementnew_1_out_17, and_6_out);
  or or_7 (or_7_out, twocomplementnew_1_out_15, and_7_out);
  or or_8 (or_8_out, twocomplementnew_1_out_10, and_8_out);
  nor nor_1 (ZERO, RESULT[0], RESULT[1], RESULT[2], RESULT[3], RESULT[4], RESULT[5], RESULT[6], NEGATIVE);

  assign RESULT[7] = NEGATIVE;
endmodule

module ALU1BIT (
  input  [2:0] in_1,
  input  in_2,
  input  in_3,
  input  in_4,
  input  in_5,
  input  in_6,
  output out_7,
  output out_8,
  output out_9
);

  wire and_1_out, nor_1_out, or_1_out, xor_1_out, xor_2_out;

  xor xor_1 (xor_1_out, in_3, in_4);
  and and_1 (and_1_out, in_2, in_3);
  or or_1 (or_1_out, in_2, in_3);
  xor xor_2 (xor_2_out, in_2, in_3);
  nor nor_1 (nor_1_out, in_2, in_3);
  Adder1bit adder1bit_1 (.a(in_2), .b(xor_1_out), .Cin(in_5), .Sum(out_9), .Cout(out_8));
  Multiplexer #(.select(3), .disabled("Z")) multiplexer_1 (
    .in0(and_1_out), .in1(or_1_out), .in2(xor_2_out), .in3(nor_1_out), .in4(out_9), .in5(in_6), .out(out_7),
    .sel(in_1));  // open: in6, in7, en

  // Notes on the sheet:
  //   ALU OPERATIONS: AND, OR, XOR, NOR, ADD/SUB, COMPARE
endmodule

module twoComplementnew (
  input  in_1,
  input  in_2,
  input  in_3,
  input  in_4,
  input  in_5,
  input  in_6,
  input  in_7,
  input  in_8,
  input  in_9,
  output out_10,
  output out_11,
  output out_12,
  output out_13,
  output out_14,
  output out_15,
  output out_16,
  output out_17
);

  wire and_1_out, and_2_out, and_3_out, and_4_out, and_5_out, and_6_out, and_7_out, and_8_out, and_9_out,
       and_10_out, and_11_out, and_12_out, and_13_out, and_14_out, and_15_out, and_16_out, and_17_out,
       and_18_out, and_19_out, and_20_out, and_21_out, and_22_out, and_23_out, not_1_out, not_2_out,
       not_3_out, not_4_out, not_5_out, not_6_out, not_7_out, not_8_out, xor_3_out, xor_5_out, xor_6_out,
       xor_8_out, xor_10_out, xor_11_out, xor_12_out, xor_13_out, xor_16_out, xor_17_out, xor_18_out,
       xor_20_out, xor_21_out, xor_22_out, xor_23_out;

  // XOR_Gate xor_1 has open pins: in0=and_4_out, in1=and_1_out, out=open
  and and_1 (and_1_out, xor_8_out, xor_3_out);
  xor xor_2 (out_10, xor_3_out, xor_8_out);
  xor xor_3 (xor_3_out, and_6_out, and_2_out);
  and and_2 (and_2_out, xor_10_out, xor_5_out);
  xor xor_4 (out_15, xor_5_out, xor_10_out);
  xor xor_5 (xor_5_out, and_7_out, and_3_out);
  and and_3 (and_3_out, xor_13_out, xor_6_out);
  xor xor_6 (xor_6_out, and_10_out, and_5_out);
  xor xor_7 (out_17, xor_6_out, xor_13_out);
  and and_4 (and_4_out, 1'b0, not_1_out);
  xor xor_8 (xor_8_out, 1'b0, not_1_out);
  and and_5 (and_5_out, xor_16_out, xor_11_out);
  and and_6 (and_6_out, 1'b0, not_2_out);
  xor xor_9 (out_13, xor_11_out, xor_16_out);
  xor xor_10 (xor_10_out, 1'b0, not_2_out);
  xor xor_11 (xor_11_out, and_11_out, and_8_out);
  xor xor_12 (xor_12_out, and_15_out, and_9_out);
  and and_7 (and_7_out, 1'b0, not_3_out);
  xor xor_13 (xor_13_out, 1'b0, not_3_out);
  and and_8 (and_8_out, xor_18_out, xor_12_out);
  and and_9 (and_9_out, xor_20_out, xor_17_out);
  and and_10 (and_10_out, 1'b0, not_4_out);
  xor xor_14 (out_11, xor_12_out, xor_18_out);
  xor xor_15 (out_16, xor_17_out, xor_20_out);
  xor xor_16 (xor_16_out, 1'b0, not_4_out);
  xor xor_17 (xor_17_out, and_17_out, and_12_out);
  and and_11 (and_11_out, 1'b0, not_5_out);
  xor xor_18 (xor_18_out, 1'b0, not_5_out);
  and and_12 (and_12_out, xor_22_out, xor_21_out);
  and and_13 (and_13_out, in_4, in_1);
  and and_14 (and_14_out, in_1, in_8);
  not not_1 (not_1_out, and_14_out);
  not not_2 (not_2_out, and_13_out);
  and and_15 (and_15_out, 1'b0, not_6_out);
  xor xor_19 (out_14, xor_21_out, xor_22_out);
  and and_16 (and_16_out, in_1, in_3);
  not not_3 (not_3_out, in_6);
  not not_4 (not_4_out, and_16_out);
  and and_17 (and_17_out, 1'b0, not_7_out);
  xor xor_20 (xor_20_out, 1'b0, not_6_out);
  xor xor_21 (xor_21_out, and_22_out, and_20_out);
  and and_18 (and_18_out, in_1, in_7);
  and and_19 (and_19_out, in_1, in_5);
  not not_5 (not_5_out, and_19_out);
  not not_6 (not_6_out, and_18_out);
  xor xor_22 (xor_22_out, not_7_out, 1'b0);
  and and_20 (and_20_out, xor_23_out, 1'b0);
  and and_21 (and_21_out, in_1, in_2);
  not not_7 (not_7_out, and_21_out);
  not not_8 (not_8_out, and_23_out);
  and and_22 (and_22_out, 1'b1, not_8_out);
  xor xor_23 (xor_23_out, not_8_out, 1'b1);
  xor xor_24 (out_12, 1'b0, xor_23_out);
  and and_23 (and_23_out, in_1, in_9);
endmodule

module threeadder (
  input  A_3,
  input  A_2,
  input  A_1,
  input  A_0,
  output S_0,
  output S_1,
  output S_2,
  output S_3
);

  wire and_1_out, and_2_out, and_3_out, and_4_out, and_5_out, and_6_out, and_7_out, and_8_out, and_9_out,
       and_10_out, not_1_out, not_2_out, not_3_out, not_4_out, not_5_out, not_6_out, not_7_out, not_8_out;

  not not_1 (not_1_out, A_1);
  not not_2 (not_2_out, A_0);
  not not_3 (not_3_out, A_2);
  not not_4 (not_4_out, A_0);
  not not_5 (not_5_out, A_0);
  not not_6 (not_6_out, A_3);
  not not_7 (not_7_out, A_2);
  not not_8 (not_8_out, A_0);
  and and_1 (and_1_out, A_2, A_1);
  and and_2 (and_2_out, A_2, A_0);
  and and_3 (and_3_out, A_3, A_0);
  and and_4 (and_4_out, A_2, not_1_out, not_2_out);
  and and_5 (and_5_out, not_3_out, A_1);
  and and_6 (and_6_out, A_1, A_0);
  and and_7 (and_7_out, A_3, not_4_out);
  and and_8 (and_8_out, A_3, not_5_out);
  and and_9 (and_9_out, not_6_out, not_7_out, A_0);
  and and_10 (and_10_out, A_2, A_1, not_8_out);
  or or_1 (S_3, A_3, and_1_out, and_2_out);
  or or_2 (S_2, and_3_out, and_4_out);
  or or_3 (S_1, and_5_out, and_6_out, and_7_out);
  or or_4 (S_0, and_8_out, and_9_out, and_10_out);
endmodule

module \byte  (
  input  address,
  input  [7:0] data,
  input  clk,
  output [7:0] output_pre,
  output [7:0] data_output
);

  wire and_1_out;
  wire [7:0] and_2_out;

  and and_1 (and_1_out, clk, address);
  D_Flip_Flop d_ff_1 (.D(and_2_out[7]), .clk(and_1_out), .Q(output_pre[7]));  // open: Qn, preset, reset
  D_Flip_Flop d_ff_2 (.D(and_2_out[6]), .clk(and_1_out), .Q(output_pre[6]));  // open: Qn, preset, reset
  D_Flip_Flop d_ff_3 (.D(and_2_out[5]), .clk(and_1_out), .Q(output_pre[5]));  // open: Qn, preset, reset
  D_Flip_Flop d_ff_4 (.D(and_2_out[4]), .clk(and_1_out), .Q(output_pre[4]));  // open: Qn, preset, reset
  assign and_2_out = data & {8{address}};  // AND_Gate and_2, 8 bits wide
  D_Flip_Flop d_ff_5 (.D(and_2_out[3]), .clk(and_1_out), .Q(output_pre[3]));  // open: Qn, preset, reset
  assign data_output = output_pre & {8{address}};  // AND_Gate and_3, 8 bits wide
  D_Flip_Flop d_ff_6 (.D(and_2_out[2]), .clk(and_1_out), .Q(output_pre[2]));  // open: Qn, preset, reset
  D_Flip_Flop d_ff_7 (.D(and_2_out[1]), .clk(and_1_out), .Q(output_pre[1]));  // open: Qn, preset, reset
  D_Flip_Flop d_ff_8 (.D(and_2_out[0]), .clk(and_1_out), .Q(output_pre[0]));  // open: Qn, preset, reset
endmodule

module BCD_TO_7_SEG (
  input  in_1,
  input  in_2,
  input  in_3,
  input  in_4,
  output out_5,
  output out_6,
  output out_7,
  output d,
  output e,
  output out_10,
  output out_11
);

  wire and_1_out, and_2_out, and_3_out, and_4_out, and_5_out, and_6_out, and_7_out, and_8_out, and_9_out,
       and_10_out, and_11_out, and_12_out, and_13_out, and_14_out, and_15_out, and_16_out, not_1_out,
       not_2_out, not_3_out, not_4_out, not_5_out, not_6_out, not_7_out, not_8_out, not_9_out, not_10_out,
       not_11_out, not_12_out, not_13_out, not_14_out, not_15_out, not_16_out, not_17_out, not_18_out,
       not_19_out, not_20_out, not_21_out;

  not not_1 (not_1_out, in_2);
  not not_2 (not_2_out, in_4);
  not not_3 (not_3_out, in_2);
  not not_4 (not_4_out, in_3);
  not not_5 (not_5_out, in_4);
  not not_6 (not_6_out, in_3);
  not not_7 (not_7_out, in_2);
  not not_8 (not_8_out, in_4);
  not not_9 (not_9_out, in_2);
  not not_10 (not_10_out, in_4);
  not not_11 (not_11_out, in_3);
  not not_12 (not_12_out, in_2);
  not not_13 (not_13_out, in_4);
  not not_14 (not_14_out, in_4);
  not not_15 (not_15_out, in_3);
  not not_16 (not_16_out, in_4);
  not not_17 (not_17_out, in_3);
  not not_18 (not_18_out, in_4);
  not not_19 (not_19_out, in_2);
  not not_20 (not_20_out, in_4);
  not not_21 (not_21_out, in_3);
  and and_1 (and_1_out, not_1_out, not_2_out);
  and and_2 (and_2_out, in_2, in_4);
  and and_3 (and_3_out, not_4_out, not_5_out);
  and and_4 (and_4_out, in_3, in_4);
  or or_1 (out_7, not_6_out, in_4, in_2);
  and and_5 (and_5_out, not_7_out, not_8_out);
  and and_6 (and_6_out, not_9_out, in_3);
  and and_7 (and_7_out, in_3, not_10_out);
  and and_8 (and_8_out, in_2, not_11_out, in_4);
  and and_9 (and_9_out, not_12_out, not_13_out);
  and and_10 (and_10_out, in_3, not_14_out);
  and and_11 (and_11_out, not_15_out, not_16_out);
  and and_12 (and_12_out, in_2, not_17_out);
  and and_13 (and_13_out, in_2, not_18_out);
  and and_14 (and_14_out, not_19_out, in_3);
  and and_15 (and_15_out, in_3, not_20_out);
  and and_16 (and_16_out, in_2, not_21_out);
  or or_2 (out_5, in_3, in_1, and_1_out, and_2_out);
  or or_3 (out_6, not_3_out, and_3_out, and_4_out);
  or or_4 (e, and_9_out, and_10_out);
  or or_5 (out_10, in_1, and_11_out, and_12_out, and_13_out);
  or or_6 (out_11, in_1, and_14_out, and_15_out, and_16_out);
  or or_7 (d, in_1, and_5_out, and_6_out, and_7_out, and_8_out);
endmodule

module Display_Connect_to_Main (
  input  in_1,
  input  in_2,
  input  in_3,
  input  in_4,
  input  in_5,
  input  in_6,
  input  in_7,
  input  in_8,
  input  in_9,
  output [7:0] out_10,
  output out_11,
  output out_12,
  output out_13,
  output out_14,
  output out_15,
  output out_16,
  output out_17,
  output out_18,
  output out_19,
  output out_20,
  output out_21,
  output out_22,
  output out_23,
  output out_24,
  output out_25,
  output out_26,
  output out_27,
  output out_28,
  output out_29,
  output out_30,
  output out_31
);

  wire threeadder_1_s_0, threeadder_1_s_1, threeadder_1_s_2, threeadder_1_s_3, threeadder_2_s_0,
       threeadder_2_s_1, threeadder_2_s_2, threeadder_2_s_3, threeadder_3_s_0, threeadder_3_s_1,
       threeadder_3_s_2, threeadder_3_s_3, threeadder_4_s_0, threeadder_4_s_1, threeadder_4_s_2,
       threeadder_4_s_3, threeadder_5_s_0, threeadder_5_s_1, threeadder_5_s_2, threeadder_5_s_3,
       threeadder_6_s_0, threeadder_6_s_1, threeadder_6_s_2, threeadder_6_s_3, threeadder_7_s_0,
       threeadder_7_s_1, threeadder_7_s_2, threeadder_7_s_3;

  BCD_TO_7_SEG bcd_to_7_seg_1 (
    .in_1(1'b0), .in_2(1'b0), .in_3(threeadder_1_s_3), .in_4(threeadder_4_s_3), .out_5(out_19),
    .out_6(out_20), .out_7(out_23), .d(out_22), .e(out_21), .out_10(out_18), .out_11(out_17));
  threeadder threeadder_1 (
    .S_0(threeadder_1_s_0), .S_1(threeadder_1_s_1), .S_2(threeadder_1_s_2), .S_3(threeadder_1_s_3),
    .A_3(1'b0), .A_2(threeadder_2_s_3), .A_1(threeadder_3_s_3), .A_0(threeadder_5_s_3));
  threeadder threeadder_2 (
    .S_0(threeadder_2_s_0), .S_1(threeadder_2_s_1), .S_2(threeadder_2_s_2), .S_3(threeadder_2_s_3),
    .A_3(1'b0), .A_2(in_1), .A_1(in_2), .A_0(in_3));
  threeadder threeadder_3 (
    .S_0(threeadder_3_s_0), .S_1(threeadder_3_s_1), .S_2(threeadder_3_s_2), .S_3(threeadder_3_s_3),
    .A_3(threeadder_2_s_2), .A_2(threeadder_2_s_1), .A_1(threeadder_2_s_0), .A_0(in_4));
  threeadder threeadder_4 (
    .S_0(threeadder_4_s_0), .S_1(threeadder_4_s_1), .S_2(threeadder_4_s_2), .S_3(threeadder_4_s_3),
    .A_3(threeadder_1_s_2), .A_2(threeadder_1_s_1), .A_1(threeadder_1_s_0), .A_0(threeadder_6_s_3));
  BCD_TO_7_SEG bcd_to_7_seg_2 (
    .in_1(threeadder_4_s_2), .in_2(threeadder_4_s_1), .in_3(threeadder_4_s_0), .in_4(threeadder_7_s_3),
    .out_5(out_27), .out_6(out_28), .out_7(out_31), .d(out_30), .e(out_29), .out_10(out_26), .out_11(out_25));
  threeadder threeadder_5 (
    .S_0(threeadder_5_s_0), .S_1(threeadder_5_s_1), .S_2(threeadder_5_s_2), .S_3(threeadder_5_s_3),
    .A_3(threeadder_3_s_2), .A_2(threeadder_3_s_1), .A_1(threeadder_3_s_0), .A_0(in_5));
  threeadder threeadder_6 (
    .S_0(threeadder_6_s_0), .S_1(threeadder_6_s_1), .S_2(threeadder_6_s_2), .S_3(threeadder_6_s_3),
    .A_3(threeadder_5_s_2), .A_2(threeadder_5_s_1), .A_1(threeadder_5_s_0), .A_0(in_6));
  threeadder threeadder_7 (
    .S_0(threeadder_7_s_0), .S_1(threeadder_7_s_1), .S_2(threeadder_7_s_2), .S_3(threeadder_7_s_3),
    .A_3(threeadder_6_s_2), .A_2(threeadder_6_s_1), .A_1(threeadder_6_s_0), .A_0(in_7));
  BCD_TO_7_SEG bcd_to_7_seg_3 (
    .in_1(threeadder_7_s_2), .in_2(threeadder_7_s_1), .in_3(threeadder_7_s_0), .in_4(in_8), .out_5(out_13),
    .out_6(out_14), .out_7(out_24), .d(out_16), .e(out_15), .out_10(out_12), .out_11(out_11));
  \byte  byte_1 (
    .address(in_9), .data({in_1, in_2, in_3, in_4, in_5, in_6, in_7, in_8}), .clk(in_9), .output_pre(out_10));  // open: data_output
endmodule

module keybb (
  input  [9:0] in_1,
  output [7:0] out_2
);

  wire or_1_out, or_2_out, or_3_out, or_4_out, xor_1_out;

  ExactlyOne xor_1 (
    .out(xor_1_out), .in0(in_1[4]), .in1(in_1[0]), .in2(in_1[1]), .in3(in_1[2]), .in4(in_1[3]),
    .in5(in_1[5]), .in6(in_1[6]), .in7(in_1[7]), .in8(in_1[8]), .in9(in_1[9]));
  not not_1 (out_2[7], 1'b1);
  or or_1 (or_1_out, in_1[0], in_1[2], in_1[4], in_1[6], in_1[8]);
  and and_1 (out_2[0], xor_1_out, or_1_out);
  or or_2 (or_2_out, in_1[1], in_1[2], in_1[5], in_1[6]);
  and and_2 (out_2[1], xor_1_out, or_2_out);
  and and_3 (out_2[2], xor_1_out, or_3_out);
  or or_3 (or_3_out, in_1[3], in_1[4], in_1[5], in_1[6]);
  or or_4 (or_4_out, in_1[7], in_1[8]);
  and and_4 (out_2[3], xor_1_out, or_4_out);

  assign out_2[6:4] = {3{out_2[7]}};
endmodule

module RAM3BIT (
  input  address,
  input  [2:0] in_2,
  input  READWRITE,
  input  CLK,
  output [2:0] out_5
);

  wire and_1_out, and_2_out, and_3_out, and_4_out, and_5_out, and_6_out, and_7_out, and_8_out, and_9_out,
       not_1_out, not_2_out, not_3_out, not_4_out, not_5_out, not_6_out, not_7_out, s_r_ff_1_q, s_r_ff_2_q,
       s_r_ff_3_q;

  not not_1 (not_1_out, in_2[0]);
  not not_2 (not_2_out, in_2[1]);
  not not_3 (not_3_out, in_2[2]);
  and and_1 (and_1_out, READWRITE, in_2[0], address);
  and and_2 (and_2_out, READWRITE, in_2[1], address);
  and and_3 (and_3_out, READWRITE, in_2[2], address);
  and and_4 (and_4_out, address, not_3_out, READWRITE);
  and and_5 (and_5_out, address, not_1_out, READWRITE);
  and and_6 (and_6_out, address, not_2_out, READWRITE);
  not not_4 (not_4_out, READWRITE);
  S_R_Flip_Flop s_r_ff_1 (.clk(CLK), .Q(s_r_ff_1_q), .reset(and_5_out), .preset(and_1_out));  // open: S, R, Qn
  S_R_Flip_Flop s_r_ff_2 (.clk(CLK), .Q(s_r_ff_2_q), .reset(and_6_out), .preset(and_2_out));  // open: S, R, Qn
  S_R_Flip_Flop s_r_ff_3 (.clk(CLK), .Q(s_r_ff_3_q), .reset(and_4_out), .preset(and_3_out));  // open: S, R, Qn
  and and_7 (and_7_out, s_r_ff_1_q, not_4_out, CLK);
  and and_8 (and_8_out, s_r_ff_2_q, not_4_out, CLK);
  and and_9 (and_9_out, s_r_ff_3_q, not_4_out, CLK);
  S_R_Flip_Flop s_r_ff_4 (.Q(out_5[2]), .reset(not_5_out), .preset(and_9_out));  // open: S, R, clk, Qn
  not not_5 (not_5_out, and_9_out);
  S_R_Flip_Flop s_r_ff_5 (.Q(out_5[1]), .reset(not_6_out), .preset(and_8_out));  // open: S, R, clk, Qn
  not not_6 (not_6_out, and_8_out);
  S_R_Flip_Flop s_r_ff_6 (.Q(out_5[0]), .reset(not_7_out), .preset(and_7_out));  // open: S, R, clk, Qn
  not not_7 (not_7_out, and_7_out);

  // Notes on the sheet:
  //   addr
endmodule
module ram4bitssecure (
  input  addr,
  input  [3:0] in_2,
  input  readwrite,
  input  clk,
  output [3:0] out_5
);

  wire and_1_out, and_2_out, and_3_out, and_4_out, and_5_out, and_6_out, and_7_out, and_8_out, not_1_out,
       not_2_out, not_3_out, not_4_out, not_5_out, s_r_ff_1_q, s_r_ff_2_q, s_r_ff_3_q, s_r_ff_4_q;

  not not_1 (not_1_out, in_2[0]);
  not not_2 (not_2_out, in_2[1]);
  not not_3 (not_3_out, in_2[2]);
  not not_4 (not_4_out, in_2[3]);
  and and_1 (and_1_out, readwrite, in_2[0], addr);
  and and_2 (and_2_out, readwrite, in_2[1], addr);
  and and_3 (and_3_out, readwrite, in_2[2], addr);
  and and_4 (and_4_out, addr, not_3_out, readwrite);
  and and_5 (and_5_out, addr, not_4_out, readwrite);
  and and_6 (and_6_out, addr, not_1_out, readwrite);
  and and_7 (and_7_out, addr, not_2_out, readwrite);
  and and_8 (and_8_out, readwrite, in_2[3], addr);
  not not_5 (not_5_out, readwrite);
  S_R_Flip_Flop s_r_ff_1 (.clk(clk), .Q(s_r_ff_1_q), .reset(and_6_out), .preset(and_1_out));  // open: S, R, Qn
  S_R_Flip_Flop s_r_ff_2 (.clk(clk), .Q(s_r_ff_2_q), .reset(and_7_out), .preset(and_2_out));  // open: S, R, Qn
  S_R_Flip_Flop s_r_ff_3 (.clk(clk), .Q(s_r_ff_3_q), .reset(and_4_out), .preset(and_3_out));  // open: S, R, Qn
  S_R_Flip_Flop s_r_ff_4 (.clk(clk), .Q(s_r_ff_4_q), .reset(and_5_out), .preset(and_8_out));  // open: S, R, Qn
  and and_9 (out_5[0], s_r_ff_1_q, not_5_out, clk);
  and and_10 (out_5[1], s_r_ff_2_q, not_5_out, clk);
  and and_11 (out_5[2], s_r_ff_3_q, not_5_out, clk);
  and and_12 (out_5[3], s_r_ff_4_q, not_5_out, clk);

  // Notes on the sheet:
  //   addr
endmodule

module onebitsecure (
  input  addr,
  input  in_2,
  input  writeread,
  input  clk,
  output out_5
);

  wire and_1_out, and_2_out, not_1_out, not_2_out, s_r_ff_1_q;

  not not_1 (not_1_out, in_2);
  and and_1 (and_1_out, writeread, in_2, addr);
  and and_2 (and_2_out, addr, not_1_out, writeread);
  not not_2 (not_2_out, writeread);
  S_R_Flip_Flop s_r_ff_1 (.clk(clk), .Q(s_r_ff_1_q), .reset(and_2_out), .preset(and_1_out));  // open: S, R, Qn
  and and_3 (out_5, s_r_ff_1_q, not_2_out, clk);

  // Notes on the sheet:
  //   addr
endmodule
